// Logisim project schematic.circ as structural Verilog: 22 circuits, main circuit main
module jtag_ram8 (
  input  clk,
  input  Jen,
  input  [31:0] Din,
  input  [31:0] Jin,
  input  Wen,
  input  [2:0] Addr,
  output [31:0] Dout,
  output [31:0] Jout
);

  wire decoder_1_out0, decoder_1_out1, decoder_1_out2, decoder_1_out3, decoder_1_out4, decoder_1_out5,
       decoder_1_out6, decoder_1_out7, or_1_out, or_2_out, or_3_out, or_4_out, or_5_out, or_6_out, or_7_out,
       or_8_out;
  wire [31:0] M0, M1, M2, M3, M4, M5, M6, multiplexer_1_out, multiplexer_2_out, multiplexer_3_out,
       multiplexer_4_out, multiplexer_5_out, multiplexer_6_out, multiplexer_7_out, multiplexer_8_out;

  Decoder #(.select(3)) decoder_1 (
    .out0(decoder_1_out0), .out1(decoder_1_out1), .out2(decoder_1_out2), .out3(decoder_1_out3),
    .out4(decoder_1_out4), .out5(decoder_1_out5), .out6(decoder_1_out6), .out7(decoder_1_out7), .sel(Addr),
    .en(Wen));
  Multiplexer #(.width(32)) multiplexer_1 (.in0(Din), .in1(Jin), .out(multiplexer_1_out), .sel(Jen));
  Multiplexer #(.width(32)) multiplexer_2 (.in0(Din), .in1(M0), .out(multiplexer_2_out), .sel(Jen));
  Multiplexer #(.width(32)) multiplexer_3 (.in0(Din), .in1(M1), .out(multiplexer_3_out), .sel(Jen));
  Multiplexer #(.width(32)) multiplexer_4 (.in0(Din), .in1(M2), .out(multiplexer_4_out), .sel(Jen));
  Multiplexer #(.width(32)) multiplexer_5 (.in0(Din), .in1(M3), .out(multiplexer_5_out), .sel(Jen));
  Multiplexer #(.width(32)) multiplexer_6 (.in0(Din), .in1(M4), .out(multiplexer_6_out), .sel(Jen));
  Multiplexer #(.width(32)) multiplexer_7 (.in0(Din), .in1(M5), .out(multiplexer_7_out), .sel(Jen));
  Multiplexer #(.width(32)) multiplexer_8 (.in0(Din), .in1(M6), .out(multiplexer_8_out), .sel(Jen));
  Register #(.width(32)) register_1 (.D(multiplexer_1_out), .en(or_1_out), .clk(clk), .Q(M0));  // open: clr
  or or_1 (or_1_out, Jen, decoder_1_out0);
  Register #(.width(32)) register_2 (.D(multiplexer_2_out), .en(or_2_out), .clk(clk), .Q(M1));  // open: clr
  or or_2 (or_2_out, Jen, decoder_1_out1);
  Register #(.width(32)) register_3 (.D(multiplexer_3_out), .en(or_3_out), .clk(clk), .Q(M2));  // open: clr
  or or_3 (or_3_out, Jen, decoder_1_out2);
  Register #(.width(32)) register_4 (.D(multiplexer_4_out), .en(or_4_out), .clk(clk), .Q(M3));  // open: clr
  or or_4 (or_4_out, Jen, decoder_1_out3);
  Register #(.width(32)) register_5 (.D(multiplexer_5_out), .en(or_5_out), .clk(clk), .Q(M4));  // open: clr
  or or_5 (or_5_out, Jen, decoder_1_out4);
  Register #(.width(32)) register_6 (.D(multiplexer_6_out), .en(or_6_out), .clk(clk), .Q(M5));  // open: clr
  or or_6 (or_6_out, Jen, decoder_1_out5);
  Register #(.width(32)) register_7 (.D(multiplexer_7_out), .en(or_7_out), .clk(clk), .Q(M6));  // open: clr
  or or_7 (or_7_out, Jen, decoder_1_out6);
  Register #(.width(32)) register_8 (.D(multiplexer_8_out), .en(or_8_out), .clk(clk), .Q(Jout));  // open: clr
  or or_8 (or_8_out, Jen, decoder_1_out7);
  Multiplexer #(.select(3), .width(32)) multiplexer_9 (
    .in0(M0), .in1(M1), .in2(M2), .in3(M3), .in4(M4), .in5(M5), .in6(M6), .in7(Jout), .out(Dout), .sel(Addr));

  // Other names for the same wires on the sheet: M7[31:0] = Jout
endmodule

module jtag_ram64 (
  input  clk,
  input  Jen,
  input  [31:0] Din,
  input  [31:0] Jin,
  input  Wen,
  input  [5:0] Addr,
  output [31:0] Dout,
  output [31:0] Jout
);

  wire decoder_1_out0, decoder_1_out1, decoder_1_out2, decoder_1_out3, decoder_1_out4, decoder_1_out5,
       decoder_1_out6, decoder_1_out7;
  wire [31:0] b0_dout, b0_jout, b1_dout, b1_jout, b2_dout, b2_jout, b3_dout, b3_jout, b4_dout, b4_jout,
       b5_dout, b5_jout, b6_dout, b6_jout, b7_dout;

  Decoder #(.select(3)) decoder_1 (
    .out0(decoder_1_out0), .out1(decoder_1_out1), .out2(decoder_1_out2), .out3(decoder_1_out3),
    .out4(decoder_1_out4), .out5(decoder_1_out5), .out6(decoder_1_out6), .out7(decoder_1_out7),
    .sel(Addr[5:3]), .en(Wen));
  jtag_ram8 b0 (
    .clk(clk), .Jen(Jen), .Din(Din), .Jin(Jin), .Wen(decoder_1_out0), .Addr(Addr[2:0]), .Dout(b0_dout),
    .Jout(b0_jout));
  jtag_ram8 b1 (
    .clk(clk), .Jen(Jen), .Din(Din), .Jin(b0_jout), .Wen(decoder_1_out1), .Addr(Addr[2:0]), .Dout(b1_dout),
    .Jout(b1_jout));
  jtag_ram8 b2 (
    .clk(clk), .Jen(Jen), .Din(Din), .Jin(b1_jout), .Wen(decoder_1_out2), .Addr(Addr[2:0]), .Dout(b2_dout),
    .Jout(b2_jout));
  jtag_ram8 b3 (
    .clk(clk), .Jen(Jen), .Din(Din), .Jin(b2_jout), .Wen(decoder_1_out3), .Addr(Addr[2:0]), .Dout(b3_dout),
    .Jout(b3_jout));
  jtag_ram8 b4 (
    .clk(clk), .Jen(Jen), .Din(Din), .Jin(b3_jout), .Wen(decoder_1_out4), .Addr(Addr[2:0]), .Dout(b4_dout),
    .Jout(b4_jout));
  jtag_ram8 b5 (
    .clk(clk), .Jen(Jen), .Din(Din), .Jin(b4_jout), .Wen(decoder_1_out5), .Addr(Addr[2:0]), .Dout(b5_dout),
    .Jout(b5_jout));
  jtag_ram8 b6 (
    .clk(clk), .Jen(Jen), .Din(Din), .Jin(b5_jout), .Wen(decoder_1_out6), .Addr(Addr[2:0]), .Dout(b6_dout),
    .Jout(b6_jout));
  jtag_ram8 b7 (
    .clk(clk), .Jen(Jen), .Din(Din), .Jin(b6_jout), .Wen(decoder_1_out7), .Addr(Addr[2:0]), .Dout(b7_dout),
    .Jout(Jout));
  Multiplexer #(.select(3), .width(32)) multiplexer_1 (
    .in0(b0_dout), .in1(b1_dout), .in2(b2_dout), .in3(b3_dout), .in4(b4_dout), .in5(b5_dout), .in6(b6_dout),
    .in7(b7_dout), .out(Dout), .sel(Addr[5:3]));
endmodule

module jtag_ram512 (
  input  clk,
  input  Jen,
  input  [31:0] Din,
  input  [31:0] Jin,
  input  Wen,
  input  [8:0] Addr,
  output [31:0] Jout,
  output [31:0] Dout
);

  wire decoder_1_out0, decoder_1_out1, decoder_1_out2, decoder_1_out3, decoder_1_out4, decoder_1_out5,
       decoder_1_out6, decoder_1_out7;
  wire [31:0] b0_dout, b0_jout, b1_dout, b1_jout, b2_dout, b2_jout, b3_dout, b3_jout, b4_dout, b4_jout,
       b5_dout, b5_jout, b6_dout, b6_jout, b7_dout;

  Decoder #(.select(3)) decoder_1 (
    .out0(decoder_1_out0), .out1(decoder_1_out1), .out2(decoder_1_out2), .out3(decoder_1_out3),
    .out4(decoder_1_out4), .out5(decoder_1_out5), .out6(decoder_1_out6), .out7(decoder_1_out7),
    .sel(Addr[8:6]), .en(Wen));
  jtag_ram64 b0 (
    .clk(clk), .Jen(Jen), .Din(Din), .Jin(Jin), .Wen(decoder_1_out0), .Addr(Addr[5:0]), .Dout(b0_dout),
    .Jout(b0_jout));
  jtag_ram64 b1 (
    .clk(clk), .Jen(Jen), .Din(Din), .Jin(b0_jout), .Wen(decoder_1_out1), .Addr(Addr[5:0]), .Dout(b1_dout),
    .Jout(b1_jout));
  jtag_ram64 b2 (
    .clk(clk), .Jen(Jen), .Din(Din), .Jin(b1_jout), .Wen(decoder_1_out2), .Addr(Addr[5:0]), .Dout(b2_dout),
    .Jout(b2_jout));
  jtag_ram64 b3 (
    .clk(clk), .Jen(Jen), .Din(Din), .Jin(b2_jout), .Wen(decoder_1_out3), .Addr(Addr[5:0]), .Dout(b3_dout),
    .Jout(b3_jout));
  jtag_ram64 b4 (
    .clk(clk), .Jen(Jen), .Din(Din), .Jin(b3_jout), .Wen(decoder_1_out4), .Addr(Addr[5:0]), .Dout(b4_dout),
    .Jout(b4_jout));
  jtag_ram64 b5 (
    .clk(clk), .Jen(Jen), .Din(Din), .Jin(b4_jout), .Wen(decoder_1_out5), .Addr(Addr[5:0]), .Dout(b5_dout),
    .Jout(b5_jout));
  jtag_ram64 b6 (
    .clk(clk), .Jen(Jen), .Din(Din), .Jin(b5_jout), .Wen(decoder_1_out6), .Addr(Addr[5:0]), .Dout(b6_dout),
    .Jout(b6_jout));
  jtag_ram64 b7 (
    .clk(clk), .Jen(Jen), .Din(Din), .Jin(b6_jout), .Wen(decoder_1_out7), .Addr(Addr[5:0]), .Dout(b7_dout),
    .Jout(Jout));
  Multiplexer #(.select(3), .width(32)) multiplexer_1 (
    .in0(b0_dout), .in1(b1_dout), .in2(b2_dout), .in3(b3_dout), .in4(b4_dout), .in5(b5_dout), .in6(b6_dout),
    .in7(b7_dout), .out(Dout), .sel(Addr[8:6]));
endmodule

module regfile (
  input  clk,
  input  rst,
  input  [31:0] Dwrite,
  input  [4:0] Awrite,
  input  [4:0] Aread0,
  input  [4:0] Aread1,
  output [31:0] Dread0,
  output [31:0] Dread1,
  output [31:0] R1,
  output [31:0] R2,
  output [31:0] R3,
  output [31:0] R4,
  output [31:0] R5,
  output [31:0] R6,
  output [31:0] R7,
  output [31:0] R8,
  output [31:0] R9,
  output [31:0] R10,
  output [31:0] R11,
  output [31:0] R12,
  output [31:0] R13,
  output [31:0] R14,
  output [31:0] R15,
  output [31:0] R16,
  output [31:0] R17,
  output [31:0] R18,
  output [31:0] R19,
  output [31:0] R20,
  output [31:0] R21,
  output [31:0] R22,
  output [31:0] R23,
  output [31:0] R24,
  output [31:0] R25,
  output [31:0] R26,
  output [31:0] R27,
  output [31:0] R28,
  output [31:0] R29,
  output [31:0] R30,
  output [31:0] R31
);

  wire and_1_out, and_2_out, and_3_out, and_4_out, and_5_out, and_6_out, and_7_out, and_8_out, and_9_out,
       and_10_out, and_11_out, and_12_out, and_13_out, and_14_out, and_15_out, and_16_out, and_17_out,
       and_18_out, and_19_out, and_20_out, and_21_out, and_22_out, and_23_out, and_24_out, and_25_out,
       and_26_out, and_27_out, and_28_out, and_29_out, and_30_out, and_31_out, and_32_out, decoder_1_out0,
       decoder_1_out1, decoder_1_out2, decoder_1_out3, decoder_1_out4, decoder_1_out5, decoder_1_out6,
       decoder_1_out7, decoder_2_out0, decoder_2_out1, decoder_2_out2, decoder_2_out3, or_1_out, or_2_out,
       or_3_out, or_4_out, or_5_out, or_6_out, or_7_out, or_8_out, or_9_out, or_10_out, or_11_out, or_12_out,
       or_13_out, or_14_out, or_15_out, or_16_out, or_17_out, or_18_out, or_19_out, or_20_out, or_21_out,
       or_22_out, or_23_out, or_24_out, or_25_out, or_26_out, or_27_out, or_28_out, or_29_out, or_30_out,
       or_31_out, or_32_out, undriven_2, undriven_3, undriven_4, undriven_5;
  wire [31:0] multiplexer_1_out, multiplexer_2_out, multiplexer_3_out, multiplexer_4_out, multiplexer_5_out,
       multiplexer_6_out, multiplexer_7_out, multiplexer_8_out, multiplexer_9_out, undriven;

  Register #(.width(32)) register_1 (.D(undriven), .en(or_1_out), .clk(undriven_2));  // open: Q, clr
  or or_1 (or_1_out, undriven_5, and_1_out);
  and and_1 (and_1_out, undriven_4, undriven_3);
  Decoder #(.select(3)) decoder_1 (
    .out0(decoder_1_out0), .out1(decoder_1_out1), .out2(decoder_1_out2), .out3(decoder_1_out3),
    .out4(decoder_1_out4), .out5(decoder_1_out5), .out6(decoder_1_out6), .out7(decoder_1_out7),
    .sel(Awrite[4:2]));  // open: en
  Decoder #(.select(2)) decoder_2 (
    .out0(decoder_2_out0), .out1(decoder_2_out1), .out2(decoder_2_out2), .out3(decoder_2_out3),
    .sel(Awrite[1:0]));  // open: en
  Multiplexer #(.width(32)) multiplexer_1 (.in0(Dwrite), .in1({32{1'b0}}), .out(multiplexer_1_out), .sel(rst));
  and and_2 (and_2_out, decoder_2_out0, decoder_1_out1);
  and and_3 (and_3_out, decoder_2_out0, decoder_1_out2);
  and and_4 (and_4_out, decoder_2_out0, decoder_1_out3);
  and and_5 (and_5_out, decoder_2_out0, decoder_1_out4);
  and and_6 (and_6_out, decoder_2_out0, decoder_1_out5);
  and and_7 (and_7_out, decoder_2_out0, decoder_1_out6);
  and and_8 (and_8_out, decoder_2_out0, decoder_1_out7);
  Register #(.width(32)) register_2 (.D(multiplexer_1_out), .en(or_2_out), .clk(clk), .Q(R4));  // open: clr
  or or_2 (or_2_out, rst, and_2_out);
  Register #(.width(32)) register_3 (.D(multiplexer_1_out), .en(or_3_out), .clk(clk), .Q(R8));  // open: clr
  or or_3 (or_3_out, rst, and_3_out);
  Register #(.width(32)) register_4 (.D(multiplexer_1_out), .en(or_4_out), .clk(clk), .Q(R12));  // open: clr
  or or_4 (or_4_out, rst, and_4_out);
  Register #(.width(32)) register_5 (.D(multiplexer_1_out), .en(or_5_out), .clk(clk), .Q(R16));  // open: clr
  or or_5 (or_5_out, rst, and_5_out);
  Register #(.width(32)) register_6 (.D(multiplexer_1_out), .en(or_6_out), .clk(clk), .Q(R20));  // open: clr
  or or_6 (or_6_out, rst, and_6_out);
  Register #(.width(32)) register_7 (.D(multiplexer_1_out), .en(or_7_out), .clk(clk), .Q(R24));  // open: clr
  or or_7 (or_7_out, rst, and_7_out);
  Register #(.width(32)) register_8 (.D(multiplexer_1_out), .en(or_8_out), .clk(clk), .Q(R28));  // open: clr
  or or_8 (or_8_out, rst, and_8_out);
  Multiplexer #(.select(3), .width(32)) multiplexer_2 (
    .in0({32{1'b0}}), .in1(R4), .in2(R8), .in3(R12), .in4(R16), .in5(R20), .in6(R24), .in7(R28),
    .out(multiplexer_2_out), .sel(Aread0[4:2]));
  Multiplexer #(.select(3), .width(32)) multiplexer_3 (
    .in0({32{1'b0}}), .in1(R4), .in2(R8), .in3(R12), .in4(R16), .in5(R20), .in6(R24), .in7(R28),
    .out(multiplexer_3_out), .sel(Aread1[4:2]));
  and and_9 (and_9_out, decoder_2_out1, decoder_1_out0);
  and and_10 (and_10_out, decoder_2_out1, decoder_1_out1);
  and and_11 (and_11_out, decoder_2_out1, decoder_1_out2);
  and and_12 (and_12_out, decoder_2_out1, decoder_1_out3);
  and and_13 (and_13_out, decoder_2_out1, decoder_1_out4);
  and and_14 (and_14_out, decoder_2_out1, decoder_1_out5);
  and and_15 (and_15_out, decoder_2_out1, decoder_1_out6);
  and and_16 (and_16_out, decoder_2_out1, decoder_1_out7);
  Register #(.width(32)) register_9 (.D(multiplexer_1_out), .en(or_9_out), .clk(clk), .Q(R1));  // open: clr
  or or_9 (or_9_out, rst, and_9_out);
  Register #(.width(32)) register_10 (.D(multiplexer_1_out), .en(or_10_out), .clk(clk), .Q(R5));  // open: clr
  or or_10 (or_10_out, rst, and_10_out);
  Register #(.width(32)) register_11 (.D(multiplexer_1_out), .en(or_11_out), .clk(clk), .Q(R9));  // open: clr
  or or_11 (or_11_out, rst, and_11_out);
  Register #(.width(32)) register_12 (.D(multiplexer_1_out), .en(or_12_out), .clk(clk), .Q(R13));  // open: clr
  or or_12 (or_12_out, rst, and_12_out);
  Register #(.width(32)) register_13 (.D(multiplexer_1_out), .en(or_13_out), .clk(clk), .Q(R17));  // open: clr
  or or_13 (or_13_out, rst, and_13_out);
  Register #(.width(32)) register_14 (.D(multiplexer_1_out), .en(or_14_out), .clk(clk), .Q(R21));  // open: clr
  or or_14 (or_14_out, rst, and_14_out);
  Register #(.width(32)) register_15 (.D(multiplexer_1_out), .en(or_15_out), .clk(clk), .Q(R25));  // open: clr
  or or_15 (or_15_out, rst, and_15_out);
  Register #(.width(32)) register_16 (.D(multiplexer_1_out), .en(or_16_out), .clk(clk), .Q(R29));  // open: clr
  or or_16 (or_16_out, rst, and_16_out);
  Multiplexer #(.select(3), .width(32)) multiplexer_4 (
    .in0(R1), .in1(R5), .in2(R9), .in3(R13), .in4(R17), .in5(R21), .in6(R25), .in7(R29),
    .out(multiplexer_4_out), .sel(Aread0[4:2]));
  Multiplexer #(.select(3), .width(32)) multiplexer_5 (
    .in0(R1), .in1(R5), .in2(R9), .in3(R13), .in4(R17), .in5(R21), .in6(R25), .in7(R29),
    .out(multiplexer_5_out), .sel(Aread1[4:2]));
  Register #(.width(32)) register_17 (.D(multiplexer_1_out), .en(or_17_out), .clk(clk), .Q(R2));  // open: clr
  or or_17 (or_17_out, rst, and_17_out);
  and and_17 (and_17_out, decoder_2_out2, decoder_1_out0);
  Register #(.width(32)) register_18 (.D(multiplexer_1_out), .en(or_18_out), .clk(clk), .Q(R6));  // open: clr
  or or_18 (or_18_out, rst, and_18_out);
  and and_18 (and_18_out, decoder_2_out2, decoder_1_out1);
  Register #(.width(32)) register_19 (.D(multiplexer_1_out), .en(or_19_out), .clk(clk), .Q(R10));  // open: clr
  or or_19 (or_19_out, rst, and_19_out);
  and and_19 (and_19_out, decoder_2_out2, decoder_1_out2);
  Register #(.width(32)) register_20 (.D(multiplexer_1_out), .en(or_20_out), .clk(clk), .Q(R14));  // open: clr
  or or_20 (or_20_out, rst, and_20_out);
  and and_20 (and_20_out, decoder_2_out2, decoder_1_out3);
  Register #(.width(32)) register_21 (.D(multiplexer_1_out), .en(or_21_out), .clk(clk), .Q(R18));  // open: clr
  or or_21 (or_21_out, rst, and_21_out);
  and and_21 (and_21_out, decoder_2_out2, decoder_1_out4);
  Register #(.width(32)) register_22 (.D(multiplexer_1_out), .en(or_22_out), .clk(clk), .Q(R22));  // open: clr
  or or_22 (or_22_out, rst, and_22_out);
  and and_22 (and_22_out, decoder_2_out2, decoder_1_out5);
  Register #(.width(32)) register_23 (.D(multiplexer_1_out), .en(or_23_out), .clk(clk), .Q(R26));  // open: clr
  or or_23 (or_23_out, rst, and_23_out);
  and and_23 (and_23_out, decoder_2_out2, decoder_1_out6);
  Register #(.width(32)) register_24 (.D(multiplexer_1_out), .en(or_24_out), .clk(clk), .Q(R30));  // open: clr
  or or_24 (or_24_out, rst, and_24_out);
  and and_24 (and_24_out, decoder_2_out2, decoder_1_out7);
  Multiplexer #(.select(3), .width(32)) multiplexer_6 (
    .in0(R2), .in1(R6), .in2(R10), .in3(R14), .in4(R18), .in5(R22), .in6(R26), .in7(R30),
    .out(multiplexer_6_out), .sel(Aread0[4:2]));
  Multiplexer #(.select(3), .width(32)) multiplexer_7 (
    .in0(R2), .in1(R6), .in2(R10), .in3(R14), .in4(R18), .in5(R22), .in6(R26), .in7(R30),
    .out(multiplexer_7_out), .sel(Aread1[4:2]));
  Register #(.width(32)) register_25 (.D(multiplexer_1_out), .en(or_25_out), .clk(clk), .Q(R3));  // open: clr
  or or_25 (or_25_out, rst, and_25_out);
  and and_25 (and_25_out, decoder_2_out3, decoder_1_out0);
  Register #(.width(32)) register_26 (.D(multiplexer_1_out), .en(or_26_out), .clk(clk), .Q(R7));  // open: clr
  or or_26 (or_26_out, rst, and_26_out);
  and and_26 (and_26_out, decoder_2_out3, decoder_1_out1);
  Register #(.width(32)) register_27 (.D(multiplexer_1_out), .en(or_27_out), .clk(clk), .Q(R11));  // open: clr
  or or_27 (or_27_out, rst, and_27_out);
  and and_27 (and_27_out, decoder_2_out3, decoder_1_out2);
  Register #(.width(32)) register_28 (.D(multiplexer_1_out), .en(or_28_out), .clk(clk), .Q(R15));  // open: clr
  or or_28 (or_28_out, rst, and_28_out);
  and and_28 (and_28_out, decoder_2_out3, decoder_1_out3);
  Register #(.width(32)) register_29 (.D(multiplexer_1_out), .en(or_29_out), .clk(clk), .Q(R19));  // open: clr
  or or_29 (or_29_out, rst, and_29_out);
  and and_29 (and_29_out, decoder_2_out3, decoder_1_out4);
  Register #(.width(32)) register_30 (.D(multiplexer_1_out), .en(or_30_out), .clk(clk), .Q(R23));  // open: clr
  or or_30 (or_30_out, rst, and_30_out);
  and and_30 (and_30_out, decoder_2_out3, decoder_1_out5);
  Register #(.width(32)) register_31 (.D(multiplexer_1_out), .en(or_31_out), .clk(clk), .Q(R27));  // open: clr
  or or_31 (or_31_out, rst, and_31_out);
  and and_31 (and_31_out, decoder_2_out3, decoder_1_out6);
  Register #(.width(32)) register_32 (.D(multiplexer_1_out), .en(or_32_out), .clk(clk), .Q(R31));  // open: clr
  or or_32 (or_32_out, rst, and_32_out);
  and and_32 (and_32_out, decoder_2_out3, decoder_1_out7);
  Multiplexer #(.select(3), .width(32)) multiplexer_8 (
    .in0(R3), .in1(R7), .in2(R11), .in3(R15), .in4(R19), .in5(R23), .in6(R27), .in7(R31),
    .out(multiplexer_8_out), .sel(Aread0[4:2]));
  Multiplexer #(.select(3), .width(32)) multiplexer_9 (
    .in0(R3), .in1(R7), .in2(R11), .in3(R15), .in4(R19), .in5(R23), .in6(R27), .in7(R31),
    .out(multiplexer_9_out), .sel(Aread1[4:2]));
  Multiplexer #(.select(2), .width(32)) multiplexer_10 (
    .in0(multiplexer_2_out), .in1(multiplexer_4_out), .in2(multiplexer_6_out), .in3(multiplexer_8_out),
    .out(Dread0), .sel(Aread0[1:0]));
  Multiplexer #(.select(2), .width(32)) multiplexer_11 (
    .in0(multiplexer_3_out), .in1(multiplexer_5_out), .in2(multiplexer_7_out), .in3(multiplexer_9_out),
    .out(Dread1), .sel(Aread1[1:0]));

  // Notes on the sheet:
  //   Field Template
endmodule

module ALU (
  input  [31:0] a,
  input  [31:0] b,
  input  output_inc,
  input  [3:0] aluop,
  input  output_inverted,
  input  clk,
  input  rst,
  output [31:0] res_low,
  output [31:0] res_high,
  output done
);

  wire alu_csa_2_cout;
  wire [31:0] Annd, not_1_out, not_2_out, oor, xoor;
  wire [32:0] ADD;
  wire [63:0] CLOO, CLZ, diiv, MUL, multiplexer_1_out, multiplexer_3_out, not_3_out, ROTR, SLL11, SRA1, SRL1,
       SUB;

  assign not_1_out = ~b;  // NOT_Gate not_1, 32 bits wide
  assign not_2_out = ~a;  // NOT_Gate not_2, 32 bits wide
  ALU_CSA alu_csa_1 (.cin(1'b0), .A(a), .B(b), .SUM(ADD[31:0]), .cout(ADD[32]));
  ALU_CSA alu_csa_2 (.cin(1'b1), .A(a), .B(not_1_out), .SUM(SUB[31:0]), .cout(alu_csa_2_cout));
  ALU_DIV alu_div_1 (.dividend(a), .divisor(b), .clk(clk), .done(done), .quotient(diiv[31:0]), .remainder(diiv[63:32]));
  ALU_ROTATE alu_rotate_1 (.a(a), .b(b), .ouuut(ROTR));
  ALU_CLO alu_clo_1 (.A(a), .OUTTTT(CLOO));
  ALU_CLO alu_clo_2 (.A(not_2_out), .OUTTTT(CLZ));
  Multiplexer #(.select(4), .width(64)) multiplexer_1 (
    .in0({{31{1'b0}}, ADD}), .in1(SUB), .in2(MUL), .in3(diiv), .in4({{32{1'b0}}, Annd}),
    .in5({{32{1'b0}}, oor}), .in6({{32{1'b0}}, xoor}), .in7(CLOO), .in8(CLZ), .in9(SLL11), .in10(SRL1),
    .in11(SRA1), .in12(ROTR), .out(multiplexer_1_out), .sel(aluop));  // open: in13, in14, in15
  assign not_3_out = ~multiplexer_1_out;  // NOT_Gate not_3, 64 bits wide
  Multiplexer #(.width(32)) multiplexer_2 (.in0({32{1'b1}}), .in1({32{1'b0}}), .out(SUB[63:32]), .sel(alu_csa_2_cout));
  Multiplexer #(.width(64)) multiplexer_3 (
    .in0(multiplexer_1_out), .in1(not_3_out), .out(multiplexer_3_out), .sel(output_inverted));
  Adder #(.width(64)) adder_1 (
    .a({64{1'b0}}), .b(multiplexer_3_out), .out({res_high, res_low}), .cin(output_inc));  // open: cout
  ALU_SRL alu_srl_1 (.a(a), .b(b), .output1(SRL1));
  ALU_SRA alu_sra_1 (.a(a), .b(b), .output1(SRA1));
  assign oor = a | b;  // OR_Gate or_1, 32 bits wide
  assign xoor = a ^ b;  // XOR_Gate xor_1, 32 bits wide
  ALU_SLL alu_sll_1 (.a(a), .b(b), .output1(SLL11));
  assign Annd = a & b;  // AND_Gate and_1, 32 bits wide
  ALU_MUL alu_mul_1 (.b(b), .a(a), .mul_out(MUL));

  // Notes on the sheet:
  //   aluop: initial=0x9
  //   a: initial=0x45b352
endmodule

module ALU_CSA (
  input  cin,
  input  [31:0] A,
  input  [31:0] B,
  output [31:0] SUM,
  output cout
);

  wire adder_1_cout, adder_2_cout, adder_3_cout, adder_4_cout, adder_5_cout, adder_6_cout, adder_7_cout,
       multiplexer_2_out, multiplexer_4_out;
  wire [7:0] adder_2_out, adder_3_out, adder_4_out, adder_5_out, adder_6_out, adder_7_out;

  Adder adder_1 (.a(A[7:0]), .b(B[7:0]), .out(SUM[7:0]), .cin(cin), .cout(adder_1_cout));
  Adder adder_2 (.a(A[15:8]), .b(B[15:8]), .out(adder_2_out), .cout(adder_2_cout));  // open: cin
  Adder adder_3 (.a(A[15:8]), .b(B[15:8]), .out(adder_3_out), .cin(1'b1), .cout(adder_3_cout));
  Adder adder_4 (.a(A[23:16]), .b(B[23:16]), .out(adder_4_out), .cout(adder_4_cout));  // open: cin
  Adder adder_5 (.a(A[23:16]), .b(B[23:16]), .out(adder_5_out), .cin(1'b1), .cout(adder_5_cout));
  Adder adder_6 (.a(A[31:24]), .b(B[31:24]), .out(adder_6_out), .cout(adder_6_cout));  // open: cin
  Adder adder_7 (.a(A[31:24]), .b(B[31:24]), .out(adder_7_out), .cin(1'b1), .cout(adder_7_cout));
  Multiplexer #(.width(8)) multiplexer_1 (.in0(adder_2_out), .in1(adder_3_out), .out(SUM[15:8]), .sel(adder_1_cout));
  Multiplexer multiplexer_2 (.in0(adder_2_cout), .in1(adder_3_cout), .out(multiplexer_2_out), .sel(adder_1_cout));
  Multiplexer #(.width(8)) multiplexer_3 (
    .in0(adder_4_out), .in1(adder_5_out), .out(SUM[23:16]), .sel(multiplexer_2_out));
  Multiplexer multiplexer_4 (.in0(adder_4_cout), .in1(adder_5_cout), .out(multiplexer_4_out), .sel(multiplexer_2_out));
  Multiplexer #(.width(8)) multiplexer_5 (
    .in0(adder_6_out), .in1(adder_7_out), .out(SUM[31:24]), .sel(multiplexer_4_out));
  Multiplexer multiplexer_6 (.in0(adder_6_cout), .in1(adder_7_cout), .out(cout), .sel(multiplexer_4_out));
endmodule

module ALU_SRL (
  input  [31:0] a,
  input  [31:0] b,
  output [63:0] output1
);

  wire comparator_1_eq;
  wire [4:0] subtractor_1_out;
  wire [26:0] subtractor_1_out_2;
  wire [63:0] multiplexer_1_out, shifter_1_out, shifter_2_out, shifter_3_out;

  Shifter #(.shift("lr"), .width(64)) shifter_1 (.in({{32{1'b0}}, a}), .\dist (6'b000001), .out(shifter_1_out));
  Subtractor #(.width(32)) subtractor_1 (
    .a(b), .b(32'h1), .out({subtractor_1_out_2, subtractor_1_out}));  // open: bin, bout
  Shifter #(.shift("lr"), .width(64)) shifter_2 (
    .in(shifter_1_out), .\dist ({1'b0, subtractor_1_out}), .out(shifter_2_out));
  Shifter #(.shift("lr"), .width(64)) shifter_3 (.in({{32{1'b0}}, a}), .\dist ({1'b0, b[4:0]}), .out(shifter_3_out));
  Multiplexer #(.width(64)) multiplexer_1 (
    .in0(shifter_2_out), .in1(shifter_3_out), .out(multiplexer_1_out), .sel(b[0]));
  Comparator #(.width(5)) comparator_1 (.a(b[4:0]), .b({5{1'b0}}), .eq(comparator_1_eq));  // open: gt, lt
  Multiplexer #(.width(64)) multiplexer_2 (
    .in0(multiplexer_1_out), .in1({{32{1'b0}}, a}), .out(output1), .sel(comparator_1_eq));
endmodule

module ALU_SRA (
  input  [31:0] a,
  input  [31:0] b,
  output [63:0] output1
);

  wire comparator_1_eq;
  wire [4:0] bit_extender_2_out;
  wire [5:0] subtractor_1_out;
  wire [25:0] subtractor_1_out_2;
  wire [31:0] multiplexer_3_out;
  wire [63:0] bit_extender_1_out, multiplexer_1_out, shifter_1_out, shifter_2_out, shifter_3_out;

  assign bit_extender_1_out = {{32{a[31]}}, a};  // Bit_Extender bit_extender_1
  Bit_Extender #(.in_width(32), .out_width(5), .\type ("zero")) bit_extender_2 (.in(b), .out(bit_extender_2_out));
  Shifter #(.shift("lr"), .width(64)) shifter_1 (.in(bit_extender_1_out), .\dist (6'b000001), .out(shifter_1_out));
  Shifter #(.shift("lr"), .width(64)) shifter_2 (.in(shifter_1_out), .\dist (subtractor_1_out), .out(shifter_2_out));
  Subtractor #(.width(32)) subtractor_1 (
    .a({{27{1'b0}}, bit_extender_2_out}), .b(32'h1), .out({subtractor_1_out_2, subtractor_1_out}));  // open: bin, bout
  Shifter #(.shift("lr"), .width(64)) shifter_3 (
    .in(bit_extender_1_out), .\dist ({1'b0, bit_extender_2_out}), .out(shifter_3_out));
  Multiplexer #(.width(64)) multiplexer_1 (
    .in0(shifter_2_out), .in1(shifter_3_out), .out(multiplexer_1_out), .sel(bit_extender_2_out[0]));
  Multiplexer #(.width(32)) multiplexer_2 (.in0({32{1'b0}}), .in1({32{1'b1}}), .out(output1[63:32]), .sel(output1[31]));
  Comparator #(.mode("unsigned"), .width(6)) comparator_1 (
    .a({1'b0, bit_extender_2_out}), .b({6{1'b0}}), .eq(comparator_1_eq));  // open: gt, lt
  Multiplexer #(.width(64)) multiplexer_3 (
    .in0(multiplexer_1_out), .in1(bit_extender_1_out), .out({multiplexer_3_out, output1[31:0]}),
    .sel(comparator_1_eq));
endmodule

module ALU_ROTATE (
  input  [31:0] a,
  input  [31:0] b,
  output [63:0] ouuut
);

  wire [31:0] subtractor_1_out;
  wire [63:0] alu_sll_1_output1, alu_srl_1_output1;
  wire [63:32] or_1_out;

  Subtractor #(.width(32)) subtractor_1 (.a(32'h20), .b(b), .out(subtractor_1_out));  // open: bin, bout
  ALU_SRL alu_srl_1 (.a(a), .b(b), .output1(alu_srl_1_output1));
  ALU_SLL alu_sll_1 (.a(a), .b(subtractor_1_out), .output1(alu_sll_1_output1));
  assign {or_1_out, ouuut[31:0]} = alu_srl_1_output1 | alu_sll_1_output1;  // OR_Gate or_1, 64 bits wide

  assign ouuut[63:32] = {32{1'b0}};
endmodule

module ALU_MUL (
  input  [31:0] b,
  input  [31:0] a,
  output [63:0] mul_out
);

  wire [63:0] alu_csavea_1_sum, alu_csavea_2_sum, alu_csavea_3_sum, alu_csavea_4_sum, alu_csavea_5_sum,
       alu_csavea_6_sum, alu_csavea_7_sum, alu_csavea_8_sum, alu_csavea_9_sum, alu_csavea_10_sum,
       alu_csavea_11_sum, alu_csavea_12_sum, alu_csavea_13_sum, alu_csavea_14_sum, alu_csavea_15_sum,
       alu_csavea_16_sum, alu_sll_1_output1, alu_sll_2_output1, alu_sll_3_output1, alu_sll_4_output1,
       alu_sll_5_output1, alu_sll_6_output1, alu_sll_7_output1, alu_sll_8_output1, alu_sll_9_output1,
       alu_sll_10_output1, alu_sll_11_output1, alu_sll_12_output1, alu_sll_13_output1, alu_sll_14_output1,
       alu_sll_15_output1, alu_sll_16_output1, alu_sll_17_output1, alu_sll_18_output1, alu_sll_19_output1,
       alu_sll_20_output1, alu_sll_21_output1, alu_sll_22_output1, alu_sll_23_output1, alu_sll_24_output1,
       alu_sll_25_output1, alu_sll_26_output1, alu_sll_27_output1, alu_sll_28_output1, alu_sll_29_output1,
       alu_sll_30_output1, alu_sll_31_output1, alu_sll_32_output1, multiplexer_1_out, multiplexer_2_out,
       multiplexer_3_out, multiplexer_4_out, multiplexer_5_out, multiplexer_6_out, multiplexer_7_out,
       multiplexer_8_out, multiplexer_9_out, multiplexer_10_out, multiplexer_11_out, multiplexer_12_out,
       multiplexer_13_out, multiplexer_14_out, multiplexer_15_out, multiplexer_16_out, multiplexer_17_out,
       multiplexer_18_out, multiplexer_19_out, multiplexer_20_out, multiplexer_21_out, multiplexer_22_out,
       multiplexer_23_out, multiplexer_24_out, multiplexer_25_out, multiplexer_26_out, multiplexer_27_out,
       multiplexer_28_out, multiplexer_29_out, multiplexer_30_out, multiplexer_31_out, multiplexer_32_out;

  ALU_SLL alu_sll_1 (.a(a), .b({32{1'b0}}), .output1(alu_sll_1_output1));
  ALU_SLL alu_sll_2 (.a(a), .b(32'h1), .output1(alu_sll_2_output1));
  ALU_SLL alu_sll_3 (.a(a), .b(32'h2), .output1(alu_sll_3_output1));
  ALU_SLL alu_sll_4 (.a(a), .b(32'h3), .output1(alu_sll_4_output1));
  ALU_SLL alu_sll_5 (.a(a), .b(32'h4), .output1(alu_sll_5_output1));
  ALU_SLL alu_sll_6 (.a(a), .b(32'h5), .output1(alu_sll_6_output1));
  ALU_SLL alu_sll_7 (.a(a), .b(32'h6), .output1(alu_sll_7_output1));
  ALU_SLL alu_sll_8 (.a(a), .b(32'h7), .output1(alu_sll_8_output1));
  ALU_SLL alu_sll_9 (.a(a), .b(32'h8), .output1(alu_sll_9_output1));
  ALU_SLL alu_sll_10 (.a(a), .b(32'h9), .output1(alu_sll_10_output1));
  ALU_SLL alu_sll_11 (.a(a), .b(32'ha), .output1(alu_sll_11_output1));
  ALU_SLL alu_sll_12 (.a(a), .b(32'hb), .output1(alu_sll_12_output1));
  ALU_SLL alu_sll_13 (.a(a), .b(32'hc), .output1(alu_sll_13_output1));
  ALU_SLL alu_sll_14 (.a(a), .b(32'hd), .output1(alu_sll_14_output1));
  ALU_SLL alu_sll_15 (.a(a), .b(32'he), .output1(alu_sll_15_output1));
  ALU_SLL alu_sll_16 (.a(a), .b(32'hf), .output1(alu_sll_16_output1));
  ALU_SLL alu_sll_17 (.a(a), .b(32'h10), .output1(alu_sll_17_output1));
  ALU_SLL alu_sll_18 (.a(a), .b(32'h11), .output1(alu_sll_18_output1));
  ALU_SLL alu_sll_19 (.a(a), .b(32'h12), .output1(alu_sll_19_output1));
  ALU_SLL alu_sll_20 (.a(a), .b(32'h13), .output1(alu_sll_20_output1));
  ALU_SLL alu_sll_21 (.a(a), .b(32'h14), .output1(alu_sll_21_output1));
  ALU_SLL alu_sll_22 (.a(a), .b(32'h15), .output1(alu_sll_22_output1));
  ALU_SLL alu_sll_23 (.a(a), .b(32'h16), .output1(alu_sll_23_output1));
  ALU_SLL alu_sll_24 (.a(a), .b(32'h17), .output1(alu_sll_24_output1));
  ALU_SLL alu_sll_25 (.a(a), .b(32'h18), .output1(alu_sll_25_output1));
  ALU_SLL alu_sll_26 (.a(a), .b(32'h19), .output1(alu_sll_26_output1));
  ALU_SLL alu_sll_27 (.a(a), .b(32'h1a), .output1(alu_sll_27_output1));
  ALU_SLL alu_sll_28 (.a(a), .b(32'h1b), .output1(alu_sll_28_output1));
  ALU_SLL alu_sll_29 (.a(a), .b(32'h1c), .output1(alu_sll_29_output1));
  ALU_SLL alu_sll_30 (.a(a), .b(32'h1d), .output1(alu_sll_30_output1));
  ALU_SLL alu_sll_31 (.a(a), .b(32'h1e), .output1(alu_sll_31_output1));
  ALU_SLL alu_sll_32 (.a(a), .b(32'h1f), .output1(alu_sll_32_output1));
  Multiplexer #(.width(64)) multiplexer_1 (
    .in0({64{1'b0}}), .in1(alu_sll_1_output1), .out(multiplexer_1_out), .sel(b[0]));
  Multiplexer #(.width(64)) multiplexer_2 (
    .in0({64{1'b0}}), .in1(alu_sll_2_output1), .out(multiplexer_2_out), .sel(b[1]));
  Multiplexer #(.width(64)) multiplexer_3 (
    .in0({64{1'b0}}), .in1(alu_sll_3_output1), .out(multiplexer_3_out), .sel(b[2]));
  Multiplexer #(.width(64)) multiplexer_4 (
    .in0({64{1'b0}}), .in1(alu_sll_4_output1), .out(multiplexer_4_out), .sel(b[3]));
  Multiplexer #(.width(64)) multiplexer_5 (
    .in0({64{1'b0}}), .in1(alu_sll_5_output1), .out(multiplexer_5_out), .sel(b[4]));
  Multiplexer #(.width(64)) multiplexer_6 (
    .in0({64{1'b0}}), .in1(alu_sll_6_output1), .out(multiplexer_6_out), .sel(b[5]));
  Multiplexer #(.width(64)) multiplexer_7 (
    .in0({64{1'b0}}), .in1(alu_sll_7_output1), .out(multiplexer_7_out), .sel(b[6]));
  Multiplexer #(.width(64)) multiplexer_8 (
    .in0({64{1'b0}}), .in1(alu_sll_8_output1), .out(multiplexer_8_out), .sel(b[7]));
  Multiplexer #(.width(64)) multiplexer_9 (
    .in0({64{1'b0}}), .in1(alu_sll_9_output1), .out(multiplexer_9_out), .sel(b[8]));
  Multiplexer #(.width(64)) multiplexer_10 (
    .in0({64{1'b0}}), .in1(alu_sll_10_output1), .out(multiplexer_10_out), .sel(b[9]));
  Multiplexer #(.width(64)) multiplexer_11 (
    .in0({64{1'b0}}), .in1(alu_sll_11_output1), .out(multiplexer_11_out), .sel(b[10]));
  Multiplexer #(.width(64)) multiplexer_12 (
    .in0({64{1'b0}}), .in1(alu_sll_12_output1), .out(multiplexer_12_out), .sel(b[11]));
  Multiplexer #(.width(64)) multiplexer_13 (
    .in0({64{1'b0}}), .in1(alu_sll_13_output1), .out(multiplexer_13_out), .sel(b[12]));
  Multiplexer #(.width(64)) multiplexer_14 (
    .in0({64{1'b0}}), .in1(alu_sll_14_output1), .out(multiplexer_14_out), .sel(b[13]));
  Multiplexer #(.width(64)) multiplexer_15 (
    .in0({64{1'b0}}), .in1(alu_sll_15_output1), .out(multiplexer_15_out), .sel(b[14]));
  Multiplexer #(.width(64)) multiplexer_16 (
    .in0({64{1'b0}}), .in1(alu_sll_16_output1), .out(multiplexer_16_out), .sel(b[15]));
  Multiplexer #(.width(64)) multiplexer_17 (
    .in0({64{1'b0}}), .in1(alu_sll_17_output1), .out(multiplexer_17_out), .sel(b[16]));
  Multiplexer #(.width(64)) multiplexer_18 (
    .in0({64{1'b0}}), .in1(alu_sll_18_output1), .out(multiplexer_18_out), .sel(b[17]));
  Multiplexer #(.width(64)) multiplexer_19 (
    .in0({64{1'b0}}), .in1(alu_sll_19_output1), .out(multiplexer_19_out), .sel(b[18]));
  Multiplexer #(.width(64)) multiplexer_20 (
    .in0({64{1'b0}}), .in1(alu_sll_20_output1), .out(multiplexer_20_out), .sel(b[19]));
  Multiplexer #(.width(64)) multiplexer_21 (
    .in0({64{1'b0}}), .in1(alu_sll_21_output1), .out(multiplexer_21_out), .sel(b[20]));
  Multiplexer #(.width(64)) multiplexer_22 (
    .in0({64{1'b0}}), .in1(alu_sll_22_output1), .out(multiplexer_22_out), .sel(b[21]));
  Multiplexer #(.width(64)) multiplexer_23 (
    .in0({64{1'b0}}), .in1(alu_sll_23_output1), .out(multiplexer_23_out), .sel(b[22]));
  Multiplexer #(.width(64)) multiplexer_24 (
    .in0({64{1'b0}}), .in1(alu_sll_24_output1), .out(multiplexer_24_out), .sel(b[23]));
  Multiplexer #(.width(64)) multiplexer_25 (
    .in0({64{1'b0}}), .in1(alu_sll_25_output1), .out(multiplexer_25_out), .sel(b[24]));
  Multiplexer #(.width(64)) multiplexer_26 (
    .in0({64{1'b0}}), .in1(alu_sll_26_output1), .out(multiplexer_26_out), .sel(b[25]));
  Multiplexer #(.width(64)) multiplexer_27 (
    .in0({64{1'b0}}), .in1(alu_sll_27_output1), .out(multiplexer_27_out), .sel(b[26]));
  Multiplexer #(.width(64)) multiplexer_28 (
    .in0({64{1'b0}}), .in1(alu_sll_28_output1), .out(multiplexer_28_out), .sel(b[27]));
  Multiplexer #(.width(64)) multiplexer_29 (
    .in0({64{1'b0}}), .in1(alu_sll_29_output1), .out(multiplexer_29_out), .sel(b[28]));
  Multiplexer #(.width(64)) multiplexer_30 (
    .in0({64{1'b0}}), .in1(alu_sll_30_output1), .out(multiplexer_30_out), .sel(b[29]));
  Multiplexer #(.width(64)) multiplexer_31 (
    .in0({64{1'b0}}), .in1(alu_sll_31_output1), .out(multiplexer_31_out), .sel(b[30]));
  Multiplexer #(.width(64)) multiplexer_32 (
    .in0({64{1'b0}}), .in1(alu_sll_32_output1), .out(multiplexer_32_out), .sel(b[31]));
  ALU_CSaveA alu_csavea_1 (.a(multiplexer_1_out), .b(multiplexer_2_out), .c(multiplexer_3_out), .sum(alu_csavea_1_sum));
  ALU_CSaveA alu_csavea_2 (.a(multiplexer_4_out), .b(multiplexer_5_out), .c(multiplexer_6_out), .sum(alu_csavea_2_sum));
  ALU_CSaveA alu_csavea_3 (.a(multiplexer_7_out), .b(multiplexer_8_out), .c(multiplexer_9_out), .sum(alu_csavea_3_sum));
  ALU_CSaveA alu_csavea_4 (
    .a(multiplexer_10_out), .b(multiplexer_11_out), .c(multiplexer_12_out), .sum(alu_csavea_4_sum));
  ALU_CSaveA alu_csavea_5 (
    .a(multiplexer_13_out), .b(multiplexer_14_out), .c(multiplexer_15_out), .sum(alu_csavea_5_sum));
  ALU_CSaveA alu_csavea_6 (
    .a(multiplexer_16_out), .b(multiplexer_17_out), .c(multiplexer_18_out), .sum(alu_csavea_6_sum));
  ALU_CSaveA alu_csavea_7 (
    .a(multiplexer_19_out), .b(multiplexer_20_out), .c(multiplexer_21_out), .sum(alu_csavea_7_sum));
  ALU_CSaveA alu_csavea_8 (
    .a(multiplexer_22_out), .b(multiplexer_23_out), .c(multiplexer_24_out), .sum(alu_csavea_8_sum));
  ALU_CSaveA alu_csavea_9 (
    .a(multiplexer_25_out), .b(multiplexer_26_out), .c(multiplexer_27_out), .sum(alu_csavea_9_sum));
  ALU_CSaveA alu_csavea_10 (
    .a(multiplexer_28_out), .b(multiplexer_29_out), .c(multiplexer_30_out), .sum(alu_csavea_10_sum));
  ALU_CSaveA alu_csavea_11 (.a(multiplexer_31_out), .b(multiplexer_32_out), .c({64{1'b0}}), .sum(alu_csavea_11_sum));
  ALU_CSaveA alu_csavea_12 (.a(alu_csavea_1_sum), .b(alu_csavea_2_sum), .c(alu_csavea_3_sum), .sum(alu_csavea_12_sum));
  ALU_CSaveA alu_csavea_13 (.a(alu_csavea_4_sum), .b(alu_csavea_5_sum), .c(alu_csavea_6_sum), .sum(alu_csavea_13_sum));
  ALU_CSaveA alu_csavea_14 (.a(alu_csavea_7_sum), .b(alu_csavea_8_sum), .c(alu_csavea_9_sum), .sum(alu_csavea_14_sum));
  ALU_CSaveA alu_csavea_15 (.a(alu_csavea_10_sum), .b(alu_csavea_11_sum), .c({64{1'b0}}), .sum(alu_csavea_15_sum));
  ALU_CSaveA alu_csavea_16 (
    .a(alu_csavea_12_sum), .b(alu_csavea_13_sum), .c(alu_csavea_14_sum), .sum(alu_csavea_16_sum));
  ALU_CSaveA alu_csavea_17 (.a(alu_csavea_16_sum), .b(alu_csavea_15_sum), .c({64{1'b0}}), .sum(mul_out));
endmodule

module ALU_DIV (
  input  [31:0] dividend,
  input  [31:0] divisor,
  input  clk,
  output done,
  output [31:0] quotient,
  output [31:0] remainder
);

  wire comparator_1_eq, comparator_2_eq, comparator_3_lt, hi, not_1_out, not_2_out, or_1_out;
  wire [0:0] q_reg_q_2;
  wire [30:0] multiplexer_3_out;
  wire [31:0] a_reg_q, multiplexer_2_out, register_1_q, register_2_q, subtractor_2_out;
  wire [31:1] q_reg_q;
  wire [31:31] multiplexer_3_out_2;
  wire [63:0] counter_q, multiplexer_1_out, subtractor_1_out;

  Register #(.width(32)) register_1 (.D(dividend), .en(1'b1), .clk(clk), .Q(register_1_q));  // open: clr
  Comparator #(.mode("unsigned"), .width(32)) comparator_1 (
    .a(dividend), .b(register_1_q), .eq(comparator_1_eq));  // open: gt, lt
  Register #(.width(32)) register_2 (.D(divisor), .en(1'b1), .clk(clk), .Q(register_2_q));  // open: clr
  not not_1 (not_1_out, comparator_1_eq);
  or or_1 (or_1_out, not_1_out, not_2_out);
  Comparator #(.mode("unsigned"), .width(32)) comparator_2 (
    .a(divisor), .b(register_2_q), .eq(comparator_2_eq));  // open: gt, lt
  Register #(.width(64)) counter (.D(multiplexer_1_out), .en(1'b1), .clk(clk), .Q(counter_q), .clr(1'b0));
  Multiplexer #(.width(64)) multiplexer_1 (
    .in0(subtractor_1_out), .in1(64'h20), .out(multiplexer_1_out), .sel(or_1_out));
  not not_2 (not_2_out, comparator_2_eq);
  Register #(.width(32)) q_reg (.D(multiplexer_2_out), .en(1'b1), .clk(clk), .Q({q_reg_q_2[0], q_reg_q}), .clr(1'b0));
  Multiplexer #(.width(32)) multiplexer_2 (
    .in0({q_reg_q, hi}), .in1(dividend), .out(multiplexer_2_out), .sel(or_1_out));
  Register #(.width(32)) a_reg (
    .D({multiplexer_3_out, q_reg_q_2[0]}), .en(1'b1), .clk(clk), .Q(a_reg_q), .clr(or_1_out));
  Subtractor #(.width(64)) subtractor_1 (.a(counter_q), .b(64'h1), .out(subtractor_1_out), .bin(1'b0));  // open: bout
  Multiplexer #(.width(32)) multiplexer_3 (
    .in0(a_reg_q), .in1(subtractor_2_out), .out({multiplexer_3_out_2[31], multiplexer_3_out}), .sel(hi));
  Subtractor #(.width(32)) subtractor_2 (.a(a_reg_q), .b(divisor), .out(subtractor_2_out), .bin(1'b0));  // open: bout
  Comparator #(.mode("unsigned"), .width(32)) comparator_3 (
    .a(a_reg_q), .b(divisor), .lt(comparator_3_lt));  // open: gt, eq
  not not_3 (hi, comparator_3_lt);
  Comparator #(.mode("unsigned"), .width(64)) comparator_4 (.a(counter_q), .b({64{1'b0}}), .eq(done));  // open: gt, lt
  Register #(.width(32)) register_3 (.D({q_reg_q, hi}), .en(done), .clk(clk), .Q(quotient), .clr(or_1_out));
  Register #(.width(32)) register_4 (
    .D({multiplexer_3_out_2[31], multiplexer_3_out}), .en(done), .clk(clk), .Q(remainder), .clr(or_1_out));
endmodule

module ALU_SLL (
  input  [31:0] a,
  input  [31:0] b,
  output [63:0] output1
);

  wire comparator_1_eq;
  wire [4:0] subtractor_1_out;
  wire [26:0] subtractor_1_out_2;
  wire [63:0] multiplexer_1_out, shifter_1_out, shifter_2_out, shifter_3_out;

  Shifter #(.width(64)) shifter_1 (.in({{32{1'b0}}, a}), .\dist (6'b000001), .out(shifter_1_out));
  Subtractor #(.width(32)) subtractor_1 (
    .a(b), .b(32'h1), .out({subtractor_1_out_2, subtractor_1_out}));  // open: bin, bout
  Shifter #(.width(64)) shifter_2 (.in(shifter_1_out), .\dist ({1'b0, subtractor_1_out}), .out(shifter_2_out));
  Shifter #(.width(64)) shifter_3 (.in({{32{1'b0}}, a}), .\dist ({1'b0, b[4:0]}), .out(shifter_3_out));
  Multiplexer #(.width(64)) multiplexer_1 (
    .in0(shifter_2_out), .in1(shifter_3_out), .out(multiplexer_1_out), .sel(b[0]));
  Comparator #(.width(5)) comparator_1 (.a(b[4:0]), .b({5{1'b0}}), .eq(comparator_1_eq));  // open: gt, lt
  Multiplexer #(.width(64)) multiplexer_2 (
    .in0(multiplexer_1_out), .in1({{32{1'b0}}, a}), .out(output1), .sel(comparator_1_eq));
endmodule

module ALU_CLO (
  input  [31:0] A,
  output [63:0] OUTTTT
);

  wire and_1_out, and_2_out, and_3_out, and_4_out, and_5_out, and_6_out, and_7_out, and_8_out, and_9_out,
       and_10_out, and_11_out, and_12_out, and_13_out, and_14_out, and_15_out, and_16_out, and_17_out,
       and_18_out, and_19_out, and_20_out, and_21_out, and_22_out, and_23_out, and_24_out, and_25_out,
       and_26_out, and_27_out, and_28_out, and_29_out, and_30_out, and_31_out, and_32_out;
  wire [1:0] adder_1_out, adder_2_out, adder_3_out, adder_4_out, adder_5_out, adder_6_out, adder_8_out,
       adder_9_out, adder_10_out, adder_11_out, adder_12_out, adder_13_out;
  wire [2:0] adder_14_out;
  wire [2:2] adder_3_cout, adder_6_cout, adder_10_cout, adder_13_cout;
  wire [3:0] adder_7_out, adder_15_out;
  wire [3:3] adder_14_cout;
  wire [4:4] adder_15_cout;

  and and_1 (and_1_out, A[30], and_2_out);
  and and_2 (and_2_out, A[31], 1'b1);
  and and_3 (and_3_out, A[29], and_1_out);
  Adder #(.width(1)) adder_1 (
    .a(and_1_out), .b(and_2_out), .out(adder_1_out[0]), .cin(and_3_out), .cout(adder_1_out[1]));
  and and_4 (and_4_out, A[27], and_5_out);
  and and_5 (and_5_out, A[28], and_3_out);
  and and_6 (and_6_out, A[26], and_4_out);
  Adder #(.width(1)) adder_2 (
    .a(and_4_out), .b(and_5_out), .out(adder_2_out[0]), .cin(and_6_out), .cout(adder_2_out[1]));
  and and_7 (and_7_out, A[24], and_8_out);
  and and_8 (and_8_out, A[25], and_6_out);
  Adder #(.width(2)) adder_3 (
    .a(adder_2_out), .b(adder_1_out), .out(adder_3_out), .cin(and_8_out), .cout(adder_3_cout[2]));
  and and_9 (and_9_out, A[22], and_10_out);
  and and_10 (and_10_out, A[23], and_7_out);
  and and_11 (and_11_out, A[21], and_9_out);
  Adder #(.width(1)) adder_4 (
    .a(and_10_out), .b(and_7_out), .out(adder_4_out[0]), .cin(and_9_out), .cout(adder_4_out[1]));
  and and_12 (and_12_out, A[19], and_13_out);
  and and_13 (and_13_out, A[20], and_11_out);
  Adder #(.width(1)) adder_5 (
    .a(and_13_out), .b(and_11_out), .out(adder_5_out[0]), .cin(and_12_out), .cout(adder_5_out[1]));
  and and_14 (and_14_out, A[18], and_12_out);
  Adder #(.width(2)) adder_6 (
    .a(adder_5_out), .b(adder_4_out), .out(adder_6_out), .cin(and_14_out), .cout(adder_6_cout[2]));
  and and_15 (and_15_out, A[16], and_16_out);
  and and_16 (and_16_out, A[17], and_14_out);
  Adder #(.width(3)) adder_7 (
    .a({adder_6_cout[2], adder_6_out}), .b({adder_3_cout[2], adder_3_out}), .out(adder_7_out[2:0]),
    .cin(and_16_out), .cout(adder_7_out[3]));
  and and_17 (and_17_out, A[14], and_18_out);
  and and_18 (and_18_out, A[15], and_15_out);
  and and_19 (and_19_out, A[13], and_17_out);
  Adder #(.width(1)) adder_8 (
    .a(and_18_out), .b(and_15_out), .out(adder_8_out[0]), .cin(and_17_out), .cout(adder_8_out[1]));
  and and_20 (and_20_out, A[11], and_21_out);
  and and_21 (and_21_out, A[12], and_19_out);
  Adder #(.width(1)) adder_9 (
    .a(and_21_out), .b(and_19_out), .out(adder_9_out[0]), .cin(and_20_out), .cout(adder_9_out[1]));
  and and_22 (and_22_out, A[10], and_20_out);
  Adder #(.width(2)) adder_10 (
    .a(adder_9_out), .b(adder_8_out), .out(adder_10_out), .cin(and_22_out), .cout(adder_10_cout[2]));
  and and_23 (and_23_out, A[8], and_24_out);
  and and_24 (and_24_out, A[9], and_22_out);
  and and_25 (and_25_out, A[6], and_26_out);
  and and_26 (and_26_out, A[7], and_23_out);
  Adder #(.width(1)) adder_11 (
    .a(and_23_out), .b(and_24_out), .out(adder_11_out[0]), .cin(and_26_out), .cout(adder_11_out[1]));
  and and_27 (and_27_out, A[5], and_25_out);
  and and_28 (and_28_out, A[3], and_29_out);
  and and_29 (and_29_out, A[4], and_27_out);
  Adder #(.width(1)) adder_12 (
    .a(and_27_out), .b(and_25_out), .out(adder_12_out[0]), .cin(and_29_out), .cout(adder_12_out[1]));
  and and_30 (and_30_out, A[2], and_28_out);
  Adder #(.width(2)) adder_13 (
    .a(adder_12_out), .b(adder_11_out), .out(adder_13_out), .cin(and_28_out), .cout(adder_13_cout[2]));
  Adder #(.width(3)) adder_14 (
    .a({adder_13_cout[2], adder_13_out}), .b({adder_10_cout[2], adder_10_out}), .out(adder_14_out),
    .cin(and_30_out), .cout(adder_14_cout[3]));
  and and_31 (and_31_out, A[0], and_32_out);
  and and_32 (and_32_out, A[1], and_30_out);
  Adder #(.width(4)) adder_15 (
    .a({adder_14_cout[3], adder_14_out}), .b(adder_7_out), .out(adder_15_out), .cin(and_32_out),
    .cout(adder_15_cout[4]));
  Adder #(.width(64)) adder_16 (
    .a({64{1'b0}}), .b({{59{1'b0}}, adder_15_cout[4], adder_15_out}), .out(OUTTTT), .cin(and_31_out));  // open: cout
endmodule

module ALU_CSaveA (
  input  [63:0] a,
  input  [63:0] b,
  input  [63:0] c,
  output [63:0] sum
);

  wire adder_1_cout, adder_1_out, adder_2_cout, adder_2_out, adder_3_cout, adder_3_out, adder_4_cout,
       adder_4_out, adder_5_cout, adder_5_out, adder_6_cout, adder_6_out, adder_7_cout, adder_7_out,
       adder_8_cout, adder_8_out, adder_9_cout, adder_9_out, adder_10_cout, adder_10_out, adder_11_cout,
       adder_11_out, adder_12_cout, adder_12_out, adder_13_cout, adder_13_out, adder_14_cout, adder_14_out,
       adder_15_cout, adder_15_out, adder_16_cout, adder_16_out, adder_17_cout, adder_17_out, adder_18_cout,
       adder_18_out, adder_19_cout, adder_19_out, adder_20_cout, adder_20_out, adder_21_cout, adder_21_out,
       adder_22_cout, adder_22_out, adder_23_cout, adder_23_out, adder_24_cout, adder_24_out, adder_25_cout,
       adder_25_out, adder_26_cout, adder_26_out, adder_27_cout, adder_27_out, adder_28_cout, adder_28_out,
       adder_29_cout, adder_29_out, adder_30_cout, adder_30_out, adder_31_cout, adder_31_out, adder_32_cout,
       adder_32_out, adder_33_cout, adder_33_out, adder_34_cout, adder_34_out, adder_35_cout, adder_35_out,
       adder_36_cout, adder_36_out, adder_37_cout, adder_37_out, adder_38_cout, adder_38_out, adder_39_cout,
       adder_39_out, adder_40_cout, adder_40_out, adder_41_cout, adder_41_out, adder_42_cout, adder_42_out,
       adder_43_cout, adder_43_out, adder_44_cout, adder_44_out, adder_45_cout, adder_45_out, adder_46_cout,
       adder_46_out, adder_47_cout, adder_47_out, adder_48_cout, adder_48_out, adder_49_cout, adder_49_out,
       adder_50_cout, adder_50_out, adder_51_cout, adder_51_out, adder_52_cout, adder_52_out, adder_53_cout,
       adder_53_out, adder_54_cout, adder_54_out, adder_55_cout, adder_55_out, adder_56_cout, adder_56_out,
       adder_57_cout, adder_57_out, adder_58_cout, adder_58_out, adder_59_cout, adder_59_out, adder_60_cout,
       adder_60_out, adder_61_cout, adder_61_out, adder_62_cout, adder_62_out, adder_63_out, adder_64_cout,
       adder_65_cout, adder_66_cout, adder_67_cout, adder_68_cout, adder_69_cout, adder_70_cout,
       adder_71_cout, adder_72_cout, adder_73_cout, adder_74_cout, adder_75_cout, adder_76_cout,
       adder_77_cout, adder_78_cout, adder_79_cout, adder_80_cout, adder_81_cout, adder_82_cout,
       adder_83_cout, adder_84_cout, adder_85_cout, adder_86_cout, adder_87_cout, adder_88_cout,
       adder_89_cout, adder_90_cout, adder_91_cout, adder_92_cout, adder_93_cout, adder_94_cout,
       adder_95_cout, adder_96_cout, adder_97_cout, adder_98_cout, adder_99_cout, adder_100_cout,
       adder_101_cout, adder_102_cout, adder_103_cout, adder_104_cout, adder_105_cout, adder_106_cout,
       adder_107_cout, adder_108_cout, adder_109_cout, adder_110_cout, adder_111_cout, adder_112_cout,
       adder_113_cout, adder_114_cout, adder_115_cout, adder_116_cout, adder_117_cout, adder_118_cout,
       adder_119_cout, adder_120_cout, adder_121_cout, adder_122_cout, adder_123_cout, adder_124_cout,
       adder_125_cout, adder_126_cout;

  Adder #(.width(1)) adder_1 (.a(b[1]), .b(c[1]), .out(adder_1_out), .cin(a[1]), .cout(adder_1_cout));
  Adder #(.width(1)) adder_2 (.a(b[2]), .b(c[2]), .out(adder_2_out), .cin(a[2]), .cout(adder_2_cout));
  Adder #(.width(1)) adder_3 (.a(b[3]), .b(c[3]), .out(adder_3_out), .cin(a[3]), .cout(adder_3_cout));
  Adder #(.width(1)) adder_4 (.a(b[4]), .b(c[4]), .out(adder_4_out), .cin(a[4]), .cout(adder_4_cout));
  Adder #(.width(1)) adder_5 (.a(b[5]), .b(c[5]), .out(adder_5_out), .cin(a[5]), .cout(adder_5_cout));
  Adder #(.width(1)) adder_6 (.a(b[6]), .b(c[6]), .out(adder_6_out), .cin(a[6]), .cout(adder_6_cout));
  Adder #(.width(1)) adder_7 (.a(b[7]), .b(c[7]), .out(adder_7_out), .cin(a[7]), .cout(adder_7_cout));
  Adder #(.width(1)) adder_8 (.a(b[8]), .b(c[8]), .out(adder_8_out), .cin(a[8]), .cout(adder_8_cout));
  Adder #(.width(1)) adder_9 (.a(b[9]), .b(c[9]), .out(adder_9_out), .cin(a[9]), .cout(adder_9_cout));
  Adder #(.width(1)) adder_10 (.a(b[10]), .b(c[10]), .out(adder_10_out), .cin(a[10]), .cout(adder_10_cout));
  Adder #(.width(1)) adder_11 (.a(b[11]), .b(c[11]), .out(adder_11_out), .cin(a[11]), .cout(adder_11_cout));
  Adder #(.width(1)) adder_12 (.a(b[12]), .b(c[12]), .out(adder_12_out), .cin(a[12]), .cout(adder_12_cout));
  Adder #(.width(1)) adder_13 (.a(b[13]), .b(c[13]), .out(adder_13_out), .cin(a[13]), .cout(adder_13_cout));
  Adder #(.width(1)) adder_14 (.a(b[14]), .b(c[14]), .out(adder_14_out), .cin(a[14]), .cout(adder_14_cout));
  Adder #(.width(1)) adder_15 (.a(b[15]), .b(c[15]), .out(adder_15_out), .cin(a[15]), .cout(adder_15_cout));
  Adder #(.width(1)) adder_16 (.a(b[16]), .b(c[16]), .out(adder_16_out), .cin(a[16]), .cout(adder_16_cout));
  Adder #(.width(1)) adder_17 (.a(b[17]), .b(c[17]), .out(adder_17_out), .cin(a[17]), .cout(adder_17_cout));
  Adder #(.width(1)) adder_18 (.a(b[18]), .b(c[18]), .out(adder_18_out), .cin(a[18]), .cout(adder_18_cout));
  Adder #(.width(1)) adder_19 (.a(b[19]), .b(c[19]), .out(adder_19_out), .cin(a[19]), .cout(adder_19_cout));
  Adder #(.width(1)) adder_20 (.a(b[20]), .b(c[20]), .out(adder_20_out), .cin(a[20]), .cout(adder_20_cout));
  Adder #(.width(1)) adder_21 (.a(b[21]), .b(c[21]), .out(adder_21_out), .cin(a[21]), .cout(adder_21_cout));
  Adder #(.width(1)) adder_22 (.a(b[22]), .b(c[22]), .out(adder_22_out), .cin(a[22]), .cout(adder_22_cout));
  Adder #(.width(1)) adder_23 (.a(b[23]), .b(c[23]), .out(adder_23_out), .cin(a[23]), .cout(adder_23_cout));
  Adder #(.width(1)) adder_24 (.a(b[24]), .b(c[24]), .out(adder_24_out), .cin(a[24]), .cout(adder_24_cout));
  Adder #(.width(1)) adder_25 (.a(b[25]), .b(c[25]), .out(adder_25_out), .cin(a[25]), .cout(adder_25_cout));
  Adder #(.width(1)) adder_26 (.a(b[26]), .b(c[26]), .out(adder_26_out), .cin(a[26]), .cout(adder_26_cout));
  Adder #(.width(1)) adder_27 (.a(b[27]), .b(c[27]), .out(adder_27_out), .cin(a[27]), .cout(adder_27_cout));
  Adder #(.width(1)) adder_28 (.a(b[28]), .b(c[28]), .out(adder_28_out), .cin(a[28]), .cout(adder_28_cout));
  Adder #(.width(1)) adder_29 (.a(b[29]), .b(c[29]), .out(adder_29_out), .cin(a[29]), .cout(adder_29_cout));
  Adder #(.width(1)) adder_30 (.a(b[30]), .b(c[30]), .out(adder_30_out), .cin(a[30]), .cout(adder_30_cout));
  Adder #(.width(1)) adder_31 (.a(b[31]), .b(c[31]), .out(adder_31_out), .cin(a[31]), .cout(adder_31_cout));
  Adder #(.width(1)) adder_32 (.a(b[32]), .b(c[32]), .out(adder_32_out), .cin(a[32]), .cout(adder_32_cout));
  Adder #(.width(1)) adder_33 (.a(b[33]), .b(c[33]), .out(adder_33_out), .cin(a[33]), .cout(adder_33_cout));
  Adder #(.width(1)) adder_34 (.a(b[34]), .b(c[34]), .out(adder_34_out), .cin(a[34]), .cout(adder_34_cout));
  Adder #(.width(1)) adder_35 (.a(b[35]), .b(c[35]), .out(adder_35_out), .cin(a[35]), .cout(adder_35_cout));
  Adder #(.width(1)) adder_36 (.a(b[36]), .b(c[36]), .out(adder_36_out), .cin(a[36]), .cout(adder_36_cout));
  Adder #(.width(1)) adder_37 (.a(b[37]), .b(c[37]), .out(adder_37_out), .cin(a[37]), .cout(adder_37_cout));
  Adder #(.width(1)) adder_38 (.a(b[38]), .b(c[38]), .out(adder_38_out), .cin(a[38]), .cout(adder_38_cout));
  Adder #(.width(1)) adder_39 (.a(b[39]), .b(c[39]), .out(adder_39_out), .cin(a[39]), .cout(adder_39_cout));
  Adder #(.width(1)) adder_40 (.a(b[40]), .b(c[40]), .out(adder_40_out), .cin(a[40]), .cout(adder_40_cout));
  Adder #(.width(1)) adder_41 (.a(b[41]), .b(c[41]), .out(adder_41_out), .cin(a[41]), .cout(adder_41_cout));
  Adder #(.width(1)) adder_42 (.a(b[42]), .b(c[42]), .out(adder_42_out), .cin(a[42]), .cout(adder_42_cout));
  Adder #(.width(1)) adder_43 (.a(b[43]), .b(c[43]), .out(adder_43_out), .cin(a[43]), .cout(adder_43_cout));
  Adder #(.width(1)) adder_44 (.a(b[44]), .b(c[44]), .out(adder_44_out), .cin(a[44]), .cout(adder_44_cout));
  Adder #(.width(1)) adder_45 (.a(b[45]), .b(c[45]), .out(adder_45_out), .cin(a[45]), .cout(adder_45_cout));
  Adder #(.width(1)) adder_46 (.a(b[46]), .b(c[46]), .out(adder_46_out), .cin(a[46]), .cout(adder_46_cout));
  Adder #(.width(1)) adder_47 (.a(b[47]), .b(c[47]), .out(adder_47_out), .cin(a[47]), .cout(adder_47_cout));
  Adder #(.width(1)) adder_48 (.a(b[48]), .b(c[48]), .out(adder_48_out), .cin(a[48]), .cout(adder_48_cout));
  Adder #(.width(1)) adder_49 (.a(b[49]), .b(c[49]), .out(adder_49_out), .cin(a[49]), .cout(adder_49_cout));
  Adder #(.width(1)) adder_50 (.a(b[50]), .b(c[50]), .out(adder_50_out), .cin(a[50]), .cout(adder_50_cout));
  Adder #(.width(1)) adder_51 (.a(b[51]), .b(c[51]), .out(adder_51_out), .cin(a[51]), .cout(adder_51_cout));
  Adder #(.width(1)) adder_52 (.a(b[52]), .b(c[52]), .out(adder_52_out), .cin(a[52]), .cout(adder_52_cout));
  Adder #(.width(1)) adder_53 (.a(b[53]), .b(c[53]), .out(adder_53_out), .cin(a[53]), .cout(adder_53_cout));
  Adder #(.width(1)) adder_54 (.a(b[54]), .b(c[54]), .out(adder_54_out), .cin(a[54]), .cout(adder_54_cout));
  Adder #(.width(1)) adder_55 (.a(b[55]), .b(c[55]), .out(adder_55_out), .cin(a[55]), .cout(adder_55_cout));
  Adder #(.width(1)) adder_56 (.a(b[56]), .b(c[56]), .out(adder_56_out), .cin(a[56]), .cout(adder_56_cout));
  Adder #(.width(1)) adder_57 (.a(b[57]), .b(c[57]), .out(adder_57_out), .cin(a[57]), .cout(adder_57_cout));
  Adder #(.width(1)) adder_58 (.a(b[58]), .b(c[58]), .out(adder_58_out), .cin(a[58]), .cout(adder_58_cout));
  Adder #(.width(1)) adder_59 (.a(b[59]), .b(c[59]), .out(adder_59_out), .cin(a[59]), .cout(adder_59_cout));
  Adder #(.width(1)) adder_60 (.a(b[60]), .b(c[60]), .out(adder_60_out), .cin(a[60]), .cout(adder_60_cout));
  Adder #(.width(1)) adder_61 (.a(b[61]), .b(c[61]), .out(adder_61_out), .cin(a[61]), .cout(adder_61_cout));
  Adder #(.width(1)) adder_62 (.a(b[62]), .b(c[62]), .out(adder_62_out), .cin(a[62]), .cout(adder_62_cout));
  Adder #(.width(1)) adder_63 (.a(b[63]), .b(c[63]), .out(adder_63_out), .cin(a[63]));  // open: cout
  Adder #(.width(1)) adder_64 (.a(b[0]), .b(c[0]), .out(sum[0]), .cin(a[0]), .cout(adder_64_cout));
  Adder #(.width(1)) adder_65 (.a(1'b0), .b(adder_1_out), .out(sum[1]), .cin(adder_64_cout), .cout(adder_65_cout));
  Adder #(.width(1)) adder_66 (
    .a(adder_1_cout), .b(adder_2_out), .out(sum[2]), .cin(adder_65_cout), .cout(adder_66_cout));
  Adder #(.width(1)) adder_67 (
    .a(adder_2_cout), .b(adder_3_out), .out(sum[3]), .cin(adder_66_cout), .cout(adder_67_cout));
  Adder #(.width(1)) adder_68 (
    .a(adder_3_cout), .b(adder_4_out), .out(sum[4]), .cin(adder_67_cout), .cout(adder_68_cout));
  Adder #(.width(1)) adder_69 (
    .a(adder_4_cout), .b(adder_5_out), .out(sum[5]), .cin(adder_68_cout), .cout(adder_69_cout));
  Adder #(.width(1)) adder_70 (
    .a(adder_5_cout), .b(adder_6_out), .out(sum[6]), .cin(adder_69_cout), .cout(adder_70_cout));
  Adder #(.width(1)) adder_71 (
    .a(adder_6_cout), .b(adder_7_out), .out(sum[7]), .cin(adder_70_cout), .cout(adder_71_cout));
  Adder #(.width(1)) adder_72 (
    .a(adder_7_cout), .b(adder_8_out), .out(sum[8]), .cin(adder_71_cout), .cout(adder_72_cout));
  Adder #(.width(1)) adder_73 (
    .a(adder_8_cout), .b(adder_9_out), .out(sum[9]), .cin(adder_72_cout), .cout(adder_73_cout));
  Adder #(.width(1)) adder_74 (
    .a(adder_9_cout), .b(adder_10_out), .out(sum[10]), .cin(adder_73_cout), .cout(adder_74_cout));
  Adder #(.width(1)) adder_75 (
    .a(adder_10_cout), .b(adder_11_out), .out(sum[11]), .cin(adder_74_cout), .cout(adder_75_cout));
  Adder #(.width(1)) adder_76 (
    .a(adder_11_cout), .b(adder_12_out), .out(sum[12]), .cin(adder_75_cout), .cout(adder_76_cout));
  Adder #(.width(1)) adder_77 (
    .a(adder_12_cout), .b(adder_13_out), .out(sum[13]), .cin(adder_76_cout), .cout(adder_77_cout));
  Adder #(.width(1)) adder_78 (
    .a(adder_13_cout), .b(adder_14_out), .out(sum[14]), .cin(adder_77_cout), .cout(adder_78_cout));
  Adder #(.width(1)) adder_79 (
    .a(adder_14_cout), .b(adder_15_out), .out(sum[15]), .cin(adder_78_cout), .cout(adder_79_cout));
  Adder #(.width(1)) adder_80 (
    .a(adder_15_cout), .b(adder_16_out), .out(sum[16]), .cin(adder_79_cout), .cout(adder_80_cout));
  Adder #(.width(1)) adder_81 (
    .a(adder_16_cout), .b(adder_17_out), .out(sum[17]), .cin(adder_80_cout), .cout(adder_81_cout));
  Adder #(.width(1)) adder_82 (
    .a(adder_17_cout), .b(adder_18_out), .out(sum[18]), .cin(adder_81_cout), .cout(adder_82_cout));
  Adder #(.width(1)) adder_83 (
    .a(adder_18_cout), .b(adder_19_out), .out(sum[19]), .cin(adder_82_cout), .cout(adder_83_cout));
  Adder #(.width(1)) adder_84 (
    .a(adder_19_cout), .b(adder_20_out), .out(sum[20]), .cin(adder_83_cout), .cout(adder_84_cout));
  Adder #(.width(1)) adder_85 (
    .a(adder_20_cout), .b(adder_21_out), .out(sum[21]), .cin(adder_84_cout), .cout(adder_85_cout));
  Adder #(.width(1)) adder_86 (
    .a(adder_21_cout), .b(adder_22_out), .out(sum[22]), .cin(adder_85_cout), .cout(adder_86_cout));
  Adder #(.width(1)) adder_87 (
    .a(adder_22_cout), .b(adder_23_out), .out(sum[23]), .cin(adder_86_cout), .cout(adder_87_cout));
  Adder #(.width(1)) adder_88 (
    .a(adder_23_cout), .b(adder_24_out), .out(sum[24]), .cin(adder_87_cout), .cout(adder_88_cout));
  Adder #(.width(1)) adder_89 (
    .a(adder_24_cout), .b(adder_25_out), .out(sum[25]), .cin(adder_88_cout), .cout(adder_89_cout));
  Adder #(.width(1)) adder_90 (
    .a(adder_25_cout), .b(adder_26_out), .out(sum[26]), .cin(adder_89_cout), .cout(adder_90_cout));
  Adder #(.width(1)) adder_91 (
    .a(adder_26_cout), .b(adder_27_out), .out(sum[27]), .cin(adder_90_cout), .cout(adder_91_cout));
  Adder #(.width(1)) adder_92 (
    .a(adder_27_cout), .b(adder_28_out), .out(sum[28]), .cin(adder_91_cout), .cout(adder_92_cout));
  Adder #(.width(1)) adder_93 (
    .a(adder_28_cout), .b(adder_29_out), .out(sum[29]), .cin(adder_92_cout), .cout(adder_93_cout));
  Adder #(.width(1)) adder_94 (
    .a(adder_29_cout), .b(adder_30_out), .out(sum[30]), .cin(adder_93_cout), .cout(adder_94_cout));
  Adder #(.width(1)) adder_95 (
    .a(adder_30_cout), .b(adder_31_out), .out(sum[31]), .cin(adder_94_cout), .cout(adder_95_cout));
  Adder #(.width(1)) adder_96 (
    .a(adder_31_cout), .b(adder_32_out), .out(sum[32]), .cin(adder_95_cout), .cout(adder_96_cout));
  Adder #(.width(1)) adder_97 (
    .a(adder_32_cout), .b(adder_33_out), .out(sum[33]), .cin(adder_96_cout), .cout(adder_97_cout));
  Adder #(.width(1)) adder_98 (
    .a(adder_33_cout), .b(adder_34_out), .out(sum[34]), .cin(adder_97_cout), .cout(adder_98_cout));
  Adder #(.width(1)) adder_99 (
    .a(adder_34_cout), .b(adder_35_out), .out(sum[35]), .cin(adder_98_cout), .cout(adder_99_cout));
  Adder #(.width(1)) adder_100 (
    .a(adder_35_cout), .b(adder_36_out), .out(sum[36]), .cin(adder_99_cout), .cout(adder_100_cout));
  Adder #(.width(1)) adder_101 (
    .a(adder_36_cout), .b(adder_37_out), .out(sum[37]), .cin(adder_100_cout), .cout(adder_101_cout));
  Adder #(.width(1)) adder_102 (
    .a(adder_37_cout), .b(adder_38_out), .out(sum[38]), .cin(adder_101_cout), .cout(adder_102_cout));
  Adder #(.width(1)) adder_103 (
    .a(adder_38_cout), .b(adder_39_out), .out(sum[39]), .cin(adder_102_cout), .cout(adder_103_cout));
  Adder #(.width(1)) adder_104 (
    .a(adder_39_cout), .b(adder_40_out), .out(sum[40]), .cin(adder_103_cout), .cout(adder_104_cout));
  Adder #(.width(1)) adder_105 (
    .a(adder_40_cout), .b(adder_41_out), .out(sum[41]), .cin(adder_104_cout), .cout(adder_105_cout));
  Adder #(.width(1)) adder_106 (
    .a(adder_41_cout), .b(adder_42_out), .out(sum[42]), .cin(adder_105_cout), .cout(adder_106_cout));
  Adder #(.width(1)) adder_107 (
    .a(adder_42_cout), .b(adder_43_out), .out(sum[43]), .cin(adder_106_cout), .cout(adder_107_cout));
  Adder #(.width(1)) adder_108 (
    .a(adder_43_cout), .b(adder_44_out), .out(sum[44]), .cin(adder_107_cout), .cout(adder_108_cout));
  Adder #(.width(1)) adder_109 (
    .a(adder_44_cout), .b(adder_45_out), .out(sum[45]), .cin(adder_108_cout), .cout(adder_109_cout));
  Adder #(.width(1)) adder_110 (
    .a(adder_45_cout), .b(adder_46_out), .out(sum[46]), .cin(adder_109_cout), .cout(adder_110_cout));
  Adder #(.width(1)) adder_111 (
    .a(adder_46_cout), .b(adder_47_out), .out(sum[47]), .cin(adder_110_cout), .cout(adder_111_cout));
  Adder #(.width(1)) adder_112 (
    .a(adder_47_cout), .b(adder_48_out), .out(sum[48]), .cin(adder_111_cout), .cout(adder_112_cout));
  Adder #(.width(1)) adder_113 (
    .a(adder_48_cout), .b(adder_49_out), .out(sum[49]), .cin(adder_112_cout), .cout(adder_113_cout));
  Adder #(.width(1)) adder_114 (
    .a(adder_49_cout), .b(adder_50_out), .out(sum[50]), .cin(adder_113_cout), .cout(adder_114_cout));
  Adder #(.width(1)) adder_115 (
    .a(adder_50_cout), .b(adder_51_out), .out(sum[51]), .cin(adder_114_cout), .cout(adder_115_cout));
  Adder #(.width(1)) adder_116 (
    .a(adder_51_cout), .b(adder_52_out), .out(sum[52]), .cin(adder_115_cout), .cout(adder_116_cout));
  Adder #(.width(1)) adder_117 (
    .a(adder_52_cout), .b(adder_53_out), .out(sum[53]), .cin(adder_116_cout), .cout(adder_117_cout));
  Adder #(.width(1)) adder_118 (
    .a(adder_53_cout), .b(adder_54_out), .out(sum[54]), .cin(adder_117_cout), .cout(adder_118_cout));
  Adder #(.width(1)) adder_119 (
    .a(adder_54_cout), .b(adder_55_out), .out(sum[55]), .cin(adder_118_cout), .cout(adder_119_cout));
  Adder #(.width(1)) adder_120 (
    .a(adder_55_cout), .b(adder_56_out), .out(sum[56]), .cin(adder_119_cout), .cout(adder_120_cout));
  Adder #(.width(1)) adder_121 (
    .a(adder_56_cout), .b(adder_57_out), .out(sum[57]), .cin(adder_120_cout), .cout(adder_121_cout));
  Adder #(.width(1)) adder_122 (
    .a(adder_57_cout), .b(adder_58_out), .out(sum[58]), .cin(adder_121_cout), .cout(adder_122_cout));
  Adder #(.width(1)) adder_123 (
    .a(adder_58_cout), .b(adder_59_out), .out(sum[59]), .cin(adder_122_cout), .cout(adder_123_cout));
  Adder #(.width(1)) adder_124 (
    .a(adder_59_cout), .b(adder_60_out), .out(sum[60]), .cin(adder_123_cout), .cout(adder_124_cout));
  Adder #(.width(1)) adder_125 (
    .a(adder_60_cout), .b(adder_61_out), .out(sum[61]), .cin(adder_124_cout), .cout(adder_125_cout));
  Adder #(.width(1)) adder_126 (
    .a(adder_61_cout), .b(adder_62_out), .out(sum[62]), .cin(adder_125_cout), .cout(adder_126_cout));
  Adder #(.width(1)) adder_127 (
    .a(adder_62_cout), .b(adder_63_out), .out(sum[63]), .cin(adder_126_cout));  // open: cout
endmodule

module main (
  input  rst,
  input  clk,
  output [31:0] R1,
  output [31:0] R2,
  output [31:0] R3,
  output [31:0] R4,
  output [31:0] R5,
  output [31:0] R6,
  output [31:0] R7,
  output [31:0] R8,
  output [31:0] R9,
  output [31:0] R10,
  output [31:0] R11,
  output [31:0] R12,
  output [31:0] R13,
  output [31:0] R14,
  output [31:0] R15,
  output [31:0] R16,
  output [31:0] R17,
  output [31:0] R18,
  output [31:0] R19,
  output [31:0] R20,
  output [31:0] R21,
  output [31:0] R22,
  output [31:0] R23,
  output [31:0] R24,
  output [31:0] Jout,
  output [31:0] R25,
  output [31:0] R26,
  output [31:0] R27,
  output [31:0] R28,
  output [31:0] R29,
  output [31:0] R30,
  output [31:0] R31,
  output InstDone
);

  wire ALUSrc, and_1_out, and_2_out, Branch, comparator_1_gt, d_ff_1_q, done, io_pro_cpu_1_bus_out,
       io_pro_peripherals_1_bus_out, io_pro_peripherals_1_keyboard_en, io_pro_peripherals_1_led_0,
       io_pro_peripherals_1_led_1, io_pro_peripherals_1_led_2, io_pro_peripherals_1_led_3,
       io_pro_peripherals_1_led_4, io_pro_peripherals_1_led_5, io_pro_peripherals_1_led_6,
       io_pro_peripherals_1_tty_en, IOIsDone, isDiv, isIO, isJal, isMfhi, isMflo, isNe, isRJ, isSll_shmt,
       isSlti, Jump, keepCurrentPC, MemRead, MemtoReg, MemWrite, or_2_out, RegDst, RegWrite, WriteData;
  wire [3:0] alu_op;
  wire [4:0] INC_shamt, multiplexer_5_out, multiplexer_6_out, multiplexer_7_out, rd, rs, rt;
  wire [5:0] funct, op;
  wire [6:0] io_pro_peripherals_1_tty_data, keyboard_1_data;
  wire [8:0] PC, pc_update_1_pc_out;
  wire [15:0] imm16, multiplexer_1_out;
  wire [31:0] adder_1_out, alu_high, alu_low, bit_extender_3_out, D_mem, DataOut, Dread0, Dread1, hi,
       I_mem_data, imm32, lo, multiplexer_2_out, multiplexer_3_out, multiplexer_4_out, multiplexer_8_out,
       multiplexer_9_out, multiplexer_10_out, multiplexer_11_out, multiplexer_12_out, RegIn, shamt;

  ROM #(.dataWidth(32)) I_mem (.addr(PC[7:0]), .data(I_mem_data));
  Register #(.width(9)) programCounter (.D(pc_update_1_pc_out), .en(1'b1), .clk(clk), .Q(PC), .clr(rst));
  Multiplexer #(.width(16)) multiplexer_1 (.in0(imm16), .in1(Dread0[15:0]), .out(multiplexer_1_out), .sel(isRJ));
  jtag_ram512 u_D_mem (
    .clk(clk), .Jen(rst), .Din(Dread1), .Jin({32{1'b0}}), .Wen(MemWrite), .Addr(alu_low[8:0]), .Jout(Jout),
    .Dout(D_mem));
  INC_decoder INC (.inc(I_mem_data), .fuunc(funct), .shamt(INC_shamt), .rd(rd), .rt(rt), .imm(imm16), .rs(rs), .op(op));
  CU Control_Unit (
    .func(funct), .op_code(op), .RegDst(RegDst), .Jump(Jump), .Branch(Branch), .MemRead(MemRead),
    .MemtoReg(MemtoReg), .MemWrite(MemWrite), .ALUSrc(ALUSrc), .RegWrite(RegWrite), .IsNe(isNe),
    .isSll_shmt(isSll_shmt), .isSlti(isSlti), .isMfhi(isMfhi), .isJal(isJal), .isMflo(isMflo), .isDiv(isDiv),
    .isIO(isIO), .isRJ(isRJ), .AlUOp(alu_op));
  PC_Update pc_update_1 (
    .PC(PC), .Branch(Branch), .isNe(isNe), .Jump(Jump), .keepCurrent(keepCurrentPC), .Eq(alu_low),
    .Imm(multiplexer_1_out), .PC_out(pc_update_1_pc_out));
  assign shamt = {{27{INC_shamt[4]}}, INC_shamt};  // Bit_Extender bit_extender_1
  assign imm32 = {{16{imm16[15]}}, imm16};  // Bit_Extender bit_extender_2
  Multiplexer #(.width(32)) multiplexer_2 (.in0(Dread1), .in1(imm32), .out(multiplexer_2_out), .sel(ALUSrc));
  Register #(.width(32)) register_1 (.D(alu_low), .en(isDiv), .clk(clk), .Q(lo));  // open: clr
  Register #(.width(32)) register_2 (.D(alu_high), .en(isDiv), .clk(clk), .Q(hi));  // open: clr
  Multiplexer #(.width(32)) multiplexer_3 (.in0(Dread0), .in1(Dread1), .out(multiplexer_3_out), .sel(isSll_shmt));
  Multiplexer #(.width(32)) multiplexer_4 (
    .in0(multiplexer_2_out), .in1(shamt), .out(multiplexer_4_out), .sel(isSll_shmt));
  D_Flip_Flop d_ff_1 (.D(done), .clk(clk), .Q(d_ff_1_q), .reset(rst));  // open: Qn, preset
  not not_1 (InstDone, keepCurrentPC);
  and and_1 (and_1_out, ~d_ff_1_q, isDiv);  // AND_Gate
  or or_1 (keepCurrentPC, and_1_out, and_2_out);
  and and_2 (and_2_out, isIO, ~IOIsDone);  // AND_Gate
  ALU alu_1 (
    .a(multiplexer_3_out), .b(multiplexer_4_out), .output_inc(1'b0), .aluop(alu_op), .output_inverted(1'b0),
    .clk(clk), .rst(rst), .res_low(alu_low), .res_high(alu_high), .done(done));
  Multiplexer #(.width(5)) multiplexer_5 (.in0(rt), .in1(rd), .out(multiplexer_5_out), .sel(RegDst));
  Multiplexer #(.width(5)) multiplexer_6 (
    .in0(multiplexer_5_out), .in1({5{1'b1}}), .out(multiplexer_6_out), .sel(isJal));
  Multiplexer #(.width(5)) multiplexer_7 (
    .in0({5{1'b0}}), .in1(multiplexer_6_out), .out(multiplexer_7_out), .sel(or_2_out));
  or or_2 (or_2_out, RegWrite, WriteData);
  Comparator #(.width(32)) comparator_1 (.a({32{1'b0}}), .b(alu_low), .gt(comparator_1_gt));  // open: eq, lt
  Multiplexer #(.width(32)) multiplexer_8 (.in0(alu_low), .in1(D_mem), .out(multiplexer_8_out), .sel(MemtoReg));
  assign bit_extender_3_out = {{31{1'b0}}, comparator_1_gt};  // Bit_Extender bit_extender_3
  Multiplexer #(.width(32)) multiplexer_9 (
    .in0(multiplexer_8_out), .in1(bit_extender_3_out), .out(multiplexer_9_out), .sel(isSlti));
  IO_pro_CPU io_pro_cpu_1 (
    .clk(clk), .isIO(isIO), .IO_index(rs), .Data_in(Dread1), .Bus_in(io_pro_peripherals_1_bus_out),
    .Bus_out(io_pro_cpu_1_bus_out), .IOIsDone(IOIsDone), .WriteData(WriteData), .Data_out(DataOut));
  Multiplexer #(.width(32)) multiplexer_10 (.in0(multiplexer_9_out), .in1(lo), .out(multiplexer_10_out), .sel(isMflo));
  Multiplexer #(.width(32)) multiplexer_11 (.in0(multiplexer_10_out), .in1(hi), .out(multiplexer_11_out), .sel(isMfhi));
  Adder #(.width(32)) adder_1 (.a({{23{1'b0}}, PC}), .b({32{1'b0}}), .out(adder_1_out), .cin(1'b1));  // open: cout
  regfile RF (
    .clk(clk), .rst(rst), .Dwrite(RegIn), .Awrite(multiplexer_7_out), .Aread0(rs), .Aread1(rt),
    .Dread0(Dread0), .Dread1(Dread1), .R1(R1), .R2(R2), .R3(R3), .R4(R4), .R5(R5), .R6(R6), .R7(R7), .R8(R8),
    .R9(R9), .R10(R10), .R11(R11), .R12(R12), .R13(R13), .R14(R14), .R15(R15), .R16(R16), .R17(R17),
    .R18(R18), .R19(R19), .R20(R20), .R21(R21), .R22(R22), .R23(R23), .R24(R24), .R25(R25), .R26(R26),
    .R27(R27), .R28(R28), .R29(R29), .R30(R30), .R31(R31));
  Multiplexer #(.width(32)) multiplexer_12 (
    .in0(multiplexer_11_out), .in1(adder_1_out), .out(multiplexer_12_out), .sel(isJal));
  Multiplexer #(.width(32)) multiplexer_13 (.in0(multiplexer_12_out), .in1(DataOut), .out(RegIn), .sel(WriteData));
  IO_pro_Peripherals io_pro_peripherals_1 (
    .clk(clk), .Bus_in(io_pro_cpu_1_bus_out), .KeyBoard_data(keyboard_1_data),
    .Bus_out(io_pro_peripherals_1_bus_out), .LED_0(io_pro_peripherals_1_led_0),
    .LED_1(io_pro_peripherals_1_led_1), .LED_2(io_pro_peripherals_1_led_2),
    .LED_3(io_pro_peripherals_1_led_3), .LED_4(io_pro_peripherals_1_led_4),
    .LED_5(io_pro_peripherals_1_led_5), .LED_6(io_pro_peripherals_1_led_6),
    .TTY_data(io_pro_peripherals_1_tty_data), .TTY_en(io_pro_peripherals_1_tty_en),
    .KeyBoard_en(io_pro_peripherals_1_keyboard_en));
  LED led_1 (.in(io_pro_peripherals_1_led_0));
  LED led_2 (.in(io_pro_peripherals_1_led_1));
  LED led_3 (.in(io_pro_peripherals_1_led_2));
  LED led_4 (.in(io_pro_peripherals_1_led_3));
  LED led_5 (.in(io_pro_peripherals_1_led_4));
  LED led_6 (.in(io_pro_peripherals_1_led_5));
  LED led_7 (.in(io_pro_peripherals_1_led_6));
  Keyboard keyboard_1 (.clk(clk), .re(io_pro_peripherals_1_keyboard_en), .data(keyboard_1_data));  // open: clr, avail
  TTY tty_1 (.data(io_pro_peripherals_1_tty_data), .clk(clk), .we(io_pro_peripherals_1_tty_en));  // open: clr

  // Notes on the sheet:
  //   contents of I_mem (hex, n*v repeats v):
  //   20020046 fd010000 fce10000 14220009 20020049 fd010000 fce10000 14220005 20020042 fd010000 fce10000
  //   14220002 8000047 2002004c 14220019 20020045 fd010000 fce10000 14220015 20020044 fd010000 fce10000
  //   14220011 20020020 fd010000 fce10000 1422000d 2002004f fd010000 fce10000 14220009 2002004e fd010000
  //   fce10000 14220005 20020020 fd010000 fce10000 14220002 8000054 20020046 14220009 20020046 fd010000
  //   fce10000 14220005 20020020 fd010000 fce10000 14220002 8000065 20020054 14220011 20020045 fd010000
  //   fce10000 1422000d 20020058 fd010000 fce10000 14220009 20020054 fd010000 fce10000 14220005 20020020
  //   fd010000 fce10000 14220002 80000a0 8000000 210826 421026 20420001 842026 20840059 a52826 ffe20000
  //   221820 a20820 a31020 1444fffb ffe00000 8000000 fd010000 fce10000 2021ffd0 421026 1022001d 20420001
  //   10220021 20420001 10220025 20420001 10220029 20420001 1022002d 20420001 10220031 20420001 10220035
  //   fd010000 fce10000 2021ffd0 421026 1022000f 20420001 10220013 20420001 10220017 20420001 1022001b
  //   20420001 1022001f 20420001 10220023 20420001 10220027 20010001 fc010000 8000000 20020000 fc010000
  //   8000000 20010002 fc210000 8000000 20020000 fc210000 8000000 20010004 fc410000 8000000 20020000
  //   fc410000 8000000 20010008 fc610000 8000000 20020000 fc610000 8000000 20010010 fc810000 8000000
  //   20020000 fc810000 8000000 20010020 fca10000 8000000 20020000 fca10000 8000000 20010040 fcc10000
  //   8000000 20020000 fcc10000 8000000 2002000a fce20000 fd010000 10220002 fce10000 80000a2 8000000
endmodule

module INC_decoder (
  input  [31:0] inc,
  output [5:0] fuunc,
  output [4:0] shamt,
  output [4:0] rd,
  output [4:0] rt,
  output [15:0] imm,
  output [4:0] rs,
  output [5:0] op
);


  assign fuunc = inc[5:0];
  assign imm = inc[15:0];
  assign op = inc[31:26];
  assign rd = inc[15:11];
  assign rs = inc[25:21];
  assign rt = inc[20:16];
  assign shamt = inc[10:6];
endmodule

module ALUOP (
  input  [5:0] op,
  input  [5:0] func,
  output [3:0] oooo
);

  wire and_1_out, and_2_out, and_3_out, and_4_out, and_5_out, and_6_out, and_7_out, and_8_out, and_9_out,
       and_10_out, and_11_out, and_12_out, and_13_out, and_14_out, and_15_out, and_16_out, and_17_out,
       and_18_out, and_19_out, comparator_1_eq, comparator_2_eq, comparator_3_eq, comparator_4_eq,
       comparator_5_eq, comparator_6_eq, comparator_7_eq, comparator_8_eq, comparator_9_eq, comparator_11_eq,
       comparator_12_eq, comparator_13_eq, comparator_14_eq, comparator_15_eq, comparator_16_eq,
       comparator_17_eq, comparator_18_eq, comparator_19_eq, comparator_20_eq, not_1_out, not_2_out,
       not_3_out, not_4_out, or_1_out, or_2_out, or_3_out, or_4_out, or_5_out, or_6_out, or_7_out, or_8_out,
       or_9_out, or_10_out, or_11_out, or_12_out, or_13_out, or_14_out, or_15_out, or_16_out, or_17_out,
       or_18_out, or_19_out, Rtype;

  Comparator #(.width(6)) comparator_1 (.a(func), .b(6'b100000), .eq(comparator_1_eq));  // open: gt, lt
  Comparator #(.width(6)) comparator_2 (.a(func), .b(6'b100010), .eq(comparator_2_eq));  // open: gt, lt
  Comparator #(.width(6)) comparator_3 (.a(func), .b(6'b100000), .eq(comparator_3_eq));  // open: gt, lt
  Comparator #(.width(6)) comparator_4 (.a(func), .b(6'b100010), .eq(comparator_4_eq));  // open: gt, lt
  Comparator #(.width(6)) comparator_5 (.a(func), .b(6'b100000), .eq(comparator_5_eq));  // open: gt, lt
  Comparator #(.width(6)) comparator_6 (.a(func), .b(6'b100100), .eq(comparator_6_eq));  // open: gt, lt
  Comparator #(.width(6)) comparator_7 (.a(func), .b(6'b100000), .eq(comparator_7_eq));  // open: gt, lt
  Comparator #(.width(6)) comparator_8 (.a(func), .b(6'b100010), .eq(comparator_8_eq));  // open: gt, lt
  and and_1 (and_1_out, Rtype, comparator_3_eq);
  and and_2 (and_2_out, Rtype, comparator_4_eq);
  and and_3 (and_3_out, Rtype, comparator_1_eq);
  and and_4 (and_4_out, Rtype, comparator_2_eq);
  Comparator #(.width(6)) comparator_9 (.a(func), .b(6'b100101), .eq(comparator_9_eq));  // open: gt, lt
  Comparator #(.width(6)) comparator_10 (.a(op), .b({6{1'b0}}), .eq(Rtype));  // open: gt, lt
  and and_5 (and_5_out, Rtype, comparator_5_eq);
  and and_6 (and_6_out, Rtype, comparator_6_eq);
  and and_7 (and_7_out, Rtype, comparator_7_eq);
  and and_8 (and_8_out, Rtype, comparator_8_eq);
  Comparator #(.width(6)) comparator_11 (.a(func), .b(6'b000110), .eq(comparator_11_eq));  // open: gt, lt
  Comparator #(.width(6)) comparator_12 (.a(func), .b(6'b000110), .eq(comparator_12_eq));  // open: gt, lt
  Comparator #(.width(6)) comparator_13 (.a(func), .b(6'b100101), .eq(comparator_13_eq));  // open: gt, lt
  Comparator #(.width(6)) comparator_14 (.a(func), .b(6'b000100), .eq(comparator_14_eq));  // open: gt, lt
  and and_9 (and_9_out, Rtype, comparator_11_eq);
  Comparator #(.width(6)) comparator_15 (.a(func), .b(6'b100100), .eq(comparator_15_eq));  // open: gt, lt
  and and_10 (and_10_out, Rtype, comparator_9_eq);
  Comparator #(.width(6)) comparator_16 (.a(func), .b(6'b100110), .eq(comparator_16_eq));  // open: gt, lt
  and and_11 (and_11_out, Rtype, comparator_12_eq);
  Comparator #(.width(6)) comparator_17 (.a(func), .b(6'b100100), .eq(comparator_17_eq));  // open: gt, lt
  and and_12 (and_12_out, Rtype, comparator_13_eq);
  or or_1 (or_1_out, and_1_out, and_2_out);
  or or_2 (or_2_out, and_3_out, and_4_out);
  and and_13 (and_13_out, Rtype, comparator_15_eq);
  or or_3 (or_3_out, and_5_out, and_6_out);
  and and_14 (and_14_out, Rtype, comparator_16_eq);
  or or_4 (or_4_out, and_7_out, and_8_out);
  and and_15 (and_15_out, Rtype, comparator_17_eq);
  or or_5 (or_5_out, or_1_out, and_16_out);
  and and_16 (and_16_out, Rtype, comparator_14_eq);
  or or_6 (or_6_out, or_2_out, and_13_out);
  or or_7 (or_7_out, or_3_out, and_14_out);
  or or_8 (or_8_out, or_4_out, and_15_out);
  or or_9 (or_9_out, or_5_out, and_9_out);
  not not_1 (not_1_out, Rtype);
  or or_10 (or_10_out, or_6_out, and_10_out);
  not not_2 (not_2_out, Rtype);
  Comparator #(.width(6)) comparator_18 (.a(func), .b(6'b100110), .eq(comparator_18_eq));  // open: gt, lt
  or or_11 (or_11_out, or_7_out, and_11_out);
  not not_3 (not_3_out, Rtype);
  or or_12 (or_12_out, or_8_out, and_12_out);
  not not_4 (not_4_out, Rtype);
  Multiplexer multiplexer_1 (.in0(1'b1), .in1(1'b0), .out(oooo[2]), .sel(or_19_out));
  or or_13 (or_13_out, or_9_out, not_1_out);
  Comparator #(.width(6)) comparator_19 (.a(func), .b(6'b000111), .eq(comparator_19_eq));  // open: gt, lt
  Multiplexer multiplexer_2 (.in0(1'b1), .in1(1'b0), .out(oooo[3]), .sel(or_17_out));
  or or_14 (or_14_out, or_10_out, not_2_out);
  and and_17 (and_17_out, Rtype, comparator_18_eq);
  Multiplexer multiplexer_3 (.in0(1'b1), .in1(1'b0), .out(oooo[0]), .sel(or_15_out));
  or or_15 (or_15_out, or_11_out, not_3_out);
  Multiplexer multiplexer_4 (.in0(1'b1), .in1(1'b0), .out(oooo[1]), .sel(or_18_out));
  or or_16 (or_16_out, or_12_out, not_4_out);
  Comparator #(.width(6)) comparator_20 (.a(func), .b(6'b000100), .eq(comparator_20_eq));  // open: gt, lt
  and and_18 (and_18_out, Rtype, comparator_19_eq);
  or or_17 (or_17_out, or_14_out, and_17_out);
  or or_18 (or_18_out, or_16_out, and_19_out);
  and and_19 (and_19_out, Rtype, comparator_20_eq);
  or or_19 (or_19_out, or_13_out, and_18_out);
endmodule

module CU (
  input  [5:0] func,
  input  [5:0] op_code,
  output RegDst,
  output Jump,
  output Branch,
  output MemRead,
  output MemtoReg,
  output MemWrite,
  output ALUSrc,
  output RegWrite,
  output IsNe,
  output isSll_shmt,
  output isSlti,
  output isMfhi,
  output isJal,
  output isMflo,
  output isDiv,
  output isIO,
  output isRJ,
  output [3:0] AlUOp
);

  wire add, addi, annd, beq, Branch_t, IsR, j, mul, mul1, nor_1_out, not_1_out, not_2_out, not_3_out,
       not_4_out, not_5_out, not_6_out, not_7_out, not_8_out, not_9_out, not_10_out, not_11_out, not_12_out,
       or1, or_10_out, sll_old, sra1, srl1, sub, xor1;

  not not_1 (not_1_out, op_code[5]);
  not not_2 (not_2_out, op_code[4]);
  not not_3 (not_3_out, op_code[3]);
  not not_4 (not_4_out, op_code[2]);
  not not_5 (not_5_out, op_code[1]);
  not not_6 (not_6_out, op_code[0]);
  and R_type (IsR, not_6_out, not_5_out, not_4_out, not_3_out, not_2_out, not_1_out);
  and u_addi (addi, not_6_out, not_5_out, not_4_out, op_code[3], not_2_out, not_1_out);
  and sw (MemWrite, op_code[0], op_code[1], not_4_out, op_code[3], not_2_out, op_code[5]);
  and lw (MemRead, op_code[5], not_2_out, not_3_out, not_4_out, op_code[1], op_code[0]);
  and bne (IsNe, not_1_out, not_2_out, not_3_out, op_code[2], not_5_out, op_code[0]);
  and slti (isSlti, not_1_out, not_2_out, op_code[3], not_4_out, op_code[1], not_6_out);
  and u_j (j, not_1_out, not_2_out, not_3_out, not_4_out, op_code[1], not_6_out);
  and u_mul1 (mul1, not_1_out, op_code[4], op_code[3], op_code[2], not_5_out, not_6_out);
  and jal (isJal, not_1_out, not_2_out, not_3_out, not_4_out, op_code[1], op_code[0]);
  and u_beq (beq, not_1_out, not_2_out, not_3_out, op_code[2], not_5_out, not_6_out);
  and IO (isIO, op_code[5], op_code[4], op_code[3], op_code[2], op_code[1], op_code[0]);
  or or_1 (RegDst, IsR, mul1);
  or or_2 (Jump, j, isJal, isRJ);
  or or_3 (Branch, IsNe, beq);
  or or_4 (Branch_t, IsNe, beq);
  or or_5 (AlUOp[1], srl1, sra1, mul, isDiv, xor1);
  or or_6 (AlUOp[2], annd, or1, xor1);
  or or_7 (AlUOp[3], sll_old, sra1, srl1, isSll_shmt);
  or or_8 (AlUOp[0], or1, Branch_t, isDiv, sub, isSll_shmt, sra1, sll_old, isSlti);
  or or_9 (ALUSrc, MemWrite, addi, MemRead, isSlti);
  and and_1 (RegWrite, or_10_out, nor_1_out);
  or or_10 (or_10_out, IsR, MemRead, mul1, addi, isSlti, isJal);
  nor nor_1 (nor_1_out, isDiv, isRJ);
  not not_7 (not_7_out, func[5]);
  not not_8 (not_8_out, func[4]);
  not not_9 (not_9_out, func[3]);
  not not_10 (not_10_out, func[2]);
  not not_11 (not_11_out, func[1]);
  not not_12 (not_12_out, func[0]);
  and u_add (add, IsR, not_12_out, not_11_out, not_10_out, not_9_out, not_8_out, func[5]);
  and u_sub (sub, IsR, not_12_out, func[1], not_10_out, not_9_out, not_8_out, func[5]);
  and u_annd (annd, IsR, not_12_out, not_11_out, func[2], not_9_out, not_8_out, func[5]);
  and u_Or1 (or1, IsR, func[0], not_11_out, func[2], not_9_out, not_8_out, func[5]);
  and u_xor1 (xor1, IsR, not_12_out, func[1], func[2], not_9_out, not_8_out, func[5]);
  and sll_SH (isSll_shmt, IsR, not_12_out, not_11_out, not_10_out, not_9_out, not_8_out, not_7_out);
  and u_srl1 (srl1, IsR, not_12_out, func[1], func[2], not_9_out, not_8_out, not_7_out);
  and u_sra1 (sra1, IsR, func[0], func[1], func[2], not_9_out, not_8_out, not_7_out);
  and mfhii (isMfhi, IsR, not_12_out, not_11_out, not_10_out, not_9_out, func[4], not_7_out);
  and mfloo (isMflo, IsR, not_12_out, func[1], not_10_out, not_9_out, func[4], not_7_out);
  and div (isDiv, IsR, not_12_out, func[1], not_10_out, func[3], func[4], not_7_out);
  and u_sll_old (sll_old, IsR, not_12_out, not_11_out, func[2], not_9_out, not_8_out, not_7_out);
  and jr (isRJ, IsR, not_12_out, not_11_out, not_10_out, func[3], not_8_out, not_7_out);
  and u_mul (mul, mul1, not_12_out, func[1], not_10_out, not_9_out, not_8_out, not_7_out);

  assign MemtoReg = MemRead;

  // Other names for the same wires on the sheet: op0 = AlUOp[0]; op1 = AlUOp[1]; op2 = AlUOp[2]; op3 = AlUOp[3];
  //   bne = IsNe; div = isDiv; jr = isRJ; mfhii = isMfhi; mfloo = isMflo; sll_SHMT = isSll_shmt; slti = isSlti
endmodule

module PC_Update (
  input  [8:0] PC,
  input  Branch,
  input  isNe,
  input  Jump,
  input  keepCurrent,
  input  [31:0] Eq,
  input  [15:0] Imm,
  output [8:0] PC_out
);

  wire and_1_out, comparator_1_eq, xor_1_out;
  wire [8:0] adder_1_out, adder_2_out, multiplexer_1_out, multiplexer_2_out;

  Adder #(.width(9)) adder_1 (.a(9'h1), .b(PC), .out(adder_1_out), .cin(1'b0));  // open: cout
  Adder #(.width(9)) adder_2 (.a(adder_1_out), .b(Imm[8:0]), .out(adder_2_out), .cin(1'b0));  // open: cout
  xor xor_1 (xor_1_out, isNe, comparator_1_eq);
  Comparator #(.width(32)) comparator_1 (.a(Eq), .b({32{1'b0}}), .eq(comparator_1_eq));  // open: gt, lt
  Multiplexer #(.width(9)) multiplexer_1 (
    .in0(adder_1_out), .in1(adder_2_out), .out(multiplexer_1_out), .sel(and_1_out));
  and and_1 (and_1_out, Branch, xor_1_out);
  Multiplexer #(.width(9)) multiplexer_2 (.in0(multiplexer_1_out), .in1(Imm[8:0]), .out(multiplexer_2_out), .sel(Jump));
  Multiplexer #(.width(9)) multiplexer_3 (.in0(multiplexer_2_out), .in1(PC), .out(PC_out), .sel(keepCurrent));
endmodule

module shift_register (
  input  load,
  input  shift,
  input  clk,
  input  rst,
  input  in0,
  input  in_6,
  input  in_7,
  input  in_8,
  input  in_9,
  input  in_10,
  input  in_11,
  input  in_12,
  input  in_13,
  input  in_14,
  input  in_15,
  input  in10,
  input  sin,
  output ou0,
  output out_19,
  output out_20,
  output out_21,
  output out_22,
  output out_23,
  output out_24,
  output out_25,
  output out_26,
  output out_27,
  output out_28,
  output ou10
);

  wire and_1_out, and_2_out, and_3_out, and_4_out, and_5_out, and_6_out, and_7_out, and_8_out, and_9_out,
       and_10_out, and_11_out, and_12_out, and_13_out, and_14_out, and_15_out, and_16_out, and_17_out,
       and_18_out, and_19_out, and_20_out, and_21_out, and_22_out, and_23_out, and_24_out, or_1_out,
       or_2_out, or_3_out, or_4_out, or_5_out, or_6_out, or_7_out, or_8_out, or_9_out, or_10_out, or_11_out,
       or_12_out, or_13_out;

  and and_1 (and_1_out, in0, load);
  and and_2 (and_2_out, in_6, load);
  and and_3 (and_3_out, in_7, load);
  and and_4 (and_4_out, in_8, load);
  and and_5 (and_5_out, in_9, load);
  and and_6 (and_6_out, in_10, load);
  and and_7 (and_7_out, in_11, load);
  and and_8 (and_8_out, in_12, load);
  and and_9 (and_9_out, in_13, load);
  and and_10 (and_10_out, in_14, load);
  and and_11 (and_11_out, in_15, load);
  and and_12 (and_12_out, in10, load);
  or or_1 (or_1_out, shift, load);
  or or_2 (or_2_out, and_1_out, and_13_out);
  and and_13 (and_13_out, shift, ~load, out_19);  // AND_Gate
  or or_3 (or_3_out, and_2_out, and_14_out);
  and and_14 (and_14_out, shift, ~load, out_20);  // AND_Gate
  or or_4 (or_4_out, and_3_out, and_15_out);
  and and_15 (and_15_out, shift, ~load, out_21);  // AND_Gate
  or or_5 (or_5_out, and_4_out, and_16_out);
  and and_16 (and_16_out, shift, ~load, out_22);  // AND_Gate
  or or_6 (or_6_out, and_5_out, and_17_out);
  and and_17 (and_17_out, shift, ~load, out_23);  // AND_Gate
  or or_7 (or_7_out, and_6_out, and_18_out);
  and and_18 (and_18_out, shift, ~load, out_24);  // AND_Gate
  or or_8 (or_8_out, and_7_out, and_19_out);
  and and_19 (and_19_out, shift, ~load, out_25);  // AND_Gate
  or or_9 (or_9_out, and_8_out, and_20_out);
  and and_20 (and_20_out, shift, ~load, out_26);  // AND_Gate
  or or_10 (or_10_out, and_9_out, and_21_out);
  and and_21 (and_21_out, shift, ~load, out_27);  // AND_Gate
  or or_11 (or_11_out, and_10_out, and_22_out);
  and and_22 (and_22_out, shift, ~load, out_28);  // AND_Gate
  or or_12 (or_12_out, and_11_out, and_23_out);
  and and_23 (and_23_out, shift, ~load, ou10);  // AND_Gate
  or or_13 (or_13_out, and_12_out, and_24_out);
  and and_24 (and_24_out, shift, ~load, sin);  // AND_Gate
  Register #(.width(1)) register_1 (.D(or_2_out), .en(or_1_out), .clk(clk), .Q(ou0), .clr(rst));
  Register #(.width(1)) register_2 (.D(or_3_out), .en(or_1_out), .clk(clk), .Q(out_19), .clr(rst));
  Register #(.width(1)) register_3 (.D(or_4_out), .en(or_1_out), .clk(clk), .Q(out_20), .clr(rst));
  Register #(.width(1)) register_4 (.D(or_5_out), .en(or_1_out), .clk(clk), .Q(out_21), .clr(rst));
  Register #(.width(1)) register_5 (.D(or_6_out), .en(or_1_out), .clk(clk), .Q(out_22), .clr(rst));
  Register #(.width(1)) register_6 (.D(or_7_out), .en(or_1_out), .clk(clk), .Q(out_23), .clr(rst));
  Register #(.width(1)) register_7 (.D(or_8_out), .en(or_1_out), .clk(clk), .Q(out_24), .clr(rst));
  Register #(.width(1)) register_8 (.D(or_9_out), .en(or_1_out), .clk(clk), .Q(out_25), .clr(rst));
  Register #(.width(1)) register_9 (.D(or_10_out), .en(or_1_out), .clk(clk), .Q(out_26), .clr(rst));
  Register #(.width(1)) register_10 (.D(or_11_out), .en(or_1_out), .clk(clk), .Q(out_27), .clr(rst));
  Register #(.width(1)) register_11 (.D(or_12_out), .en(or_1_out), .clk(clk), .Q(out_28), .clr(rst));
  Register #(.width(1)) register_12 (.D(or_13_out), .en(or_1_out), .clk(clk), .Q(ou10), .clr(rst));
endmodule

module IO_pro_CPU (
  input  clk,
  input  isIO,
  input  [4:0] IO_index,
  input  [31:0] Data_in,
  input  Bus_in,
  output Bus_out,
  output IOIsDone,
  output WriteData,
  output [31:0] Data_out
);

  wire comparator_1_eq, d_ff_1_q, d_ff_2_q, d_ff_3_q, multiplexer_1_out, not_1_out, register_1_q;

  D_Flip_Flop d_ff_1 (.D(IOIsDone), .clk(clk), .Q(d_ff_1_q));  // open: Qn, preset, reset
  D_Flip_Flop d_ff_2 (.D(isIO), .clk(clk), .Q(d_ff_2_q), .reset(d_ff_1_q));  // open: Qn, preset
  D_Flip_Flop d_ff_3 (.D(d_ff_2_q), .clk(clk), .Q(d_ff_3_q));  // open: Qn, preset, reset
  Multiplexer multiplexer_1 (.in0(d_ff_2_q), .in1(1'b0), .out(multiplexer_1_out), .sel(d_ff_3_q));
  Register #(.width(1)) register_1 (.D(IOIsDone), .clk(clk), .Q(register_1_q));  // open: en, clr
  not not_1 (not_1_out, IOIsDone);
  shift_register shift_register_1 (
    .load(multiplexer_1_out), .shift(d_ff_2_q), .clk(clk), .in0(isIO), .in_6(IO_index[0]),
    .in_7(IO_index[1]), .in_8(IO_index[2]), .in_9(IO_index[3]), .in_10(Data_in[0]), .in_11(Data_in[1]),
    .in_12(Data_in[2]), .in_13(Data_in[3]), .in_14(Data_in[4]), .in_15(Data_in[5]), .in10(Data_in[6]),
    .ou0(Bus_out));  // open: rst, sin, out_19, out_20, out_21, out_22, out_23, out_24, out_25, out_26, out_27, out_28, ou10
  shift_register shift_register_2 (
    .shift(not_1_out), .clk(clk), .rst(register_1_q), .sin(Bus_in), .ou0(IOIsDone), .out_19(Data_out[0]),
    .out_20(Data_out[1]), .out_21(Data_out[2]), .out_22(Data_out[3]), .out_23(Data_out[4]),
    .out_24(Data_out[5]), .out_25(Data_out[6]));  // open: load, in0, in_6, in_7, in_8, in_9, in_10, in_11, in_12, in_13, in_14, in_15, in10, out_26, out_27, out_28, ou10
  Comparator #(.width(5)) comparator_1 (.a(IO_index), .b(5'b01000), .eq(comparator_1_eq));  // open: gt, lt
  and and_1 (WriteData, IOIsDone, comparator_1_eq);
endmodule

module IO_pro_Peripherals (
  input  clk,
  input  Bus_in,
  input  [6:0] KeyBoard_data,
  output Bus_out,
  output LED_0,
  output LED_1,
  output LED_2,
  output LED_3,
  output LED_4,
  output LED_5,
  output LED_6,
  output [6:0] TTY_data,
  output TTY_en,
  output KeyBoard_en
);

  wire comparator_1_eq, d_ff_1_q, LED_0_t, LED_1_t, LED_2_t, LED_3_t, LED_4_t, LED_5_t, LED_6_t, LED_ALL,
       msgReceived, multiplexer_1_out, not_1_out, or_1_out, or_2_out, or_3_out, or_4_out, or_5_out, or_6_out,
       or_7_out, register_1_q, send_Messege;
  wire [3:0] lsb4;
  wire [6:0] KeyBoard_Data_t;
  wire [7:0] adder_1_out, register_2_q;

  Register #(.width(1)) register_1 (.D(msgReceived), .clk(clk), .Q(register_1_q));  // open: en, clr
  D_Flip_Flop d_ff_1 (.D(send_Messege), .clk(clk), .Q(d_ff_1_q));  // open: Qn, preset, reset
  not not_1 (not_1_out, msgReceived);
  Multiplexer multiplexer_1 (.in0(send_Messege), .in1(1'b0), .out(multiplexer_1_out), .sel(d_ff_1_q));
  shift_register shift_register_1 (
    .shift(not_1_out), .clk(clk), .rst(register_1_q), .sin(Bus_in), .ou0(msgReceived), .out_19(lsb4[0]),
    .out_20(lsb4[1]), .out_21(lsb4[2]), .out_22(lsb4[3]), .out_23(TTY_data[0]), .out_24(TTY_data[1]),
    .out_25(TTY_data[2]), .out_26(TTY_data[3]), .out_27(TTY_data[4]), .out_28(TTY_data[5]), .ou10(TTY_data[6]));  // open: load, in0, in_6, in_7, in_8, in_9, in_10, in_11, in_12, in_13, in_14, in_15, in10
  shift_register shift_register_2 (
    .load(multiplexer_1_out), .shift(send_Messege), .clk(clk), .in0(send_Messege), .in_6(KeyBoard_Data_t[0]),
    .in_7(KeyBoard_Data_t[1]), .in_8(KeyBoard_Data_t[2]), .in_9(KeyBoard_Data_t[3]),
    .in_10(KeyBoard_Data_t[4]), .in_11(KeyBoard_Data_t[5]), .in_12(KeyBoard_Data_t[6]), .ou0(Bus_out));  // open: rst, in_13, in_14, in_15, in10, sin, out_19, out_20, out_21, out_22, out_23, out_24, out_25, out_26, out_27, out_28, ou10
  Register register_2 (.D(adder_1_out), .clk(clk), .Q(register_2_q), .clr(msgReceived));  // open: en
  Adder adder_1 (.a(register_2_q), .b({8{1'b0}}), .out(adder_1_out), .cin(1'b1));  // open: cout
  Decoder #(.select(4)) decoder_1 (
    .out0(LED_0_t), .out1(LED_1_t), .out2(LED_2_t), .out3(LED_3_t), .out4(LED_4_t), .out5(LED_5_t),
    .out6(LED_6_t), .out7(TTY_en), .out8(KeyBoard_en), .out15(LED_ALL), .sel(lsb4), .en(msgReceived));  // open: out9, out10, out11, out12, out13, out14
  Register #(.width(1)) register_3 (.D(1'b1), .en(msgReceived), .clk(clk), .Q(send_Messege), .clr(comparator_1_eq));
  Comparator comparator_1 (.a(adder_1_out), .b(8'hf), .eq(comparator_1_eq));  // open: gt, lt
  Register #(.width(7)) register_4 (.D(KeyBoard_data), .en(KeyBoard_en), .clk(clk), .Q(KeyBoard_Data_t));  // open: clr
  or or_1 (or_1_out, LED_ALL, LED_0_t);
  or or_2 (or_2_out, LED_ALL, LED_1_t);
  or or_3 (or_3_out, LED_ALL, LED_2_t);
  or or_4 (or_4_out, LED_ALL, LED_3_t);
  or or_5 (or_5_out, LED_ALL, LED_4_t);
  or or_6 (or_6_out, LED_ALL, LED_5_t);
  or or_7 (or_7_out, LED_ALL, LED_6_t);
  Register #(.width(1)) register_5 (.D(TTY_data[0]), .en(or_1_out), .clk(clk), .Q(LED_0));  // open: clr
  Register #(.width(1)) register_6 (.D(TTY_data[1]), .en(or_2_out), .clk(clk), .Q(LED_1));  // open: clr
  Register #(.width(1)) register_7 (.D(TTY_data[2]), .en(or_3_out), .clk(clk), .Q(LED_2));  // open: clr
  Register #(.width(1)) register_8 (.D(TTY_data[3]), .en(or_4_out), .clk(clk), .Q(LED_3));  // open: clr
  Register #(.width(1)) register_9 (.D(TTY_data[4]), .en(or_5_out), .clk(clk), .Q(LED_4));  // open: clr
  Register #(.width(1)) register_10 (.D(TTY_data[5]), .en(or_6_out), .clk(clk), .Q(LED_5));  // open: clr
  Register #(.width(1)) register_11 (.D(TTY_data[6]), .en(or_7_out), .clk(clk), .Q(LED_6));  // open: clr

  // Other names for the same wires on the sheet: KeyBoard_0 = KeyBoard_en; data0 = TTY_data[0]; msb7[6:0] = TTY_data;
  //   data1 = TTY_data[1]; data2 = TTY_data[2]; data3 = TTY_data[3]; data4 = TTY_data[4]; data5 = TTY_data[5];
  //   data6 = TTY_data[6]; TTY_0 = TTY_en
endmodule
